// Logisim project CS1401_U201414573_朱珺_MIPSCPU_backup6.circ as structural Verilog: 23 circuits, main circuit main
module main (
  input  in_1,
  input  in_2,
  input  in_3,
  input  in_4,
  output out_5,
  output [1:0] out_6,
  output [1:0] out_7,
  output out_8
);

  wire and_1_out, and_2_out, and_3_out, and_4_out, and_5_out, and_6_out, and_8_out, and_9_out, and_10_out,
       BGEZ, bit_extender_3_out, clk, clock_1_out, clt3, clt4, clt5, clt6, clt8, clt9, clt10, clt11,
       clt12_EX, clt12_ID, clt13, clt14, clt15, clt16, clt17, clt18_ID, clt18_WB, clt19, clt20_EX, clt20_ID,
       clt_sft, control_1_ctl17, control_1_ctl18, cp0_1_im1, cp0_1_im2, cp0_1_im3, ctl1, ctl2, d_ff_1_q,
       d_ff_2_q, d_ff_3_q, d_ff_4_q, d_ff_5_q, demultiplexer_1_out1, demultiplexer_1_out2,
       demultiplexer_1_out3, equal, equal2, ID_EX_RE, ID_Mem_RE, ID_WB_RE, IE, IM1, IM2, IM3, INT, INT1_out,
       INT2_out, INT3_out, multiplexer_9_out, No_relative, not_2_out, not_3_out, not_7_out, not_8_out,
       not_9_out, not_10_out, not_11_out, not_12_out, not_13_out, or_3_out, or_4_out, or_5_out, or_7_out,
       or_8_out, or_9_out, PC_Chged, Relative;
  wire [1:0] bit_extender_2_out, mem_wb_1_byte_sel_out, multiplexer_13_out;
  wire [3:0] aluctl_1_out_4, clt7, op;
  wire [4:0] ir_1_rd_11_15, ir_1_rs_21_25, ir_1_rt_16_20, ir_2_shmat_6_10, multiplexer_2_out,
       multiplexer_3_out, Rd_WB, Rt_WB;
  wire [5:0] ir_1_funct_0_5, ir_1_op_26_31;
  wire [7:0] byte_selector_1_out_3;
  wire [15:0] ir_1_im_0_15;
  wire [23:0] control_1_ctl1;
  wire [31:0] adder_1_out, ALU_result, bit_extender_1_out, bit_extender_5_out, counter_1_q, cp0_1_epc,
       CP0_out, Din, ex_mem_1_alu_result_out, ex_mem_1_r2_out, ex_mem_1_sig_out, Ext, id_ex_1_r2_out,
       Instruct_EX, Instruct_ID, Instruct_Mem, Instruct_WB, INT_PC, jia8, main_1_reg1, main_1_reg2_2,
       main_1_s0_value, main_1_s1_value, mem_wb_1_alu_result_out, mem_wb_1_rd_out, mem_wb_1_sig_out,
       multiplexer_4_out, multiplexer_5_out, multiplexer_7_out, multiplexer_8_out, multiplexer_11_out,
       multiplexer_12_out, multiplexer_14_out, multiplexer_15_out, multiplexer_16_out, multiplexer_18_out,
       multiplexer_19_out, multiplexer_20_out, Next_PC, npc_1_out_5, num, PC_4_EX, PC_4_ID, PC_4_Mem,
       PC_4_WB, PC_EX, PC_Mem, R1, ram_1_data, register_1_q, rom_1_data, shifter_1_out, shmat, y1;
  wire [31:2] id_ex_1_sig_out, ir_2_l26_0_25;

  or or_1 (Relative, ID_WB_RE, ID_Mem_RE, ID_EX_RE);
  not not_1 (No_relative, Relative);
  Multiplexer #(.width(32), .disabled(0), .enable("false")) multiplexer_1 (
    .in0(npc_1_out_5), .in1(PC_Mem), .out(Next_PC), .sel(PC_Chged));
  Register #(.width(32), .trigger("falling")) register_1 (
    .D(Next_PC), .en(No_relative), .Q(register_1_q), .clk(clk), .clr(in_2));
  // Probe on counter_1_q
  Counter #(.width(32), .max('hffffffff), .ongoal("stay")) counter_1 (
    .load(1'b0), .D({32{1'b0}}), .count(1'b1), .Q(counter_1_q), .clk(clk), .clr(in_4));  // open: carry
  NPC npc_1 (
    .PC(register_1_q), .out_5(npc_1_out_5), .high4(ir_2_l26_0_25[31:28]), .jia8(jia8), .BGEZ(BGEZ),
    .IM(ir_1_im_0_15));
  Hex_Digit_Display hex_digit_display_1 (.value(num[27:24]));  // open: dp
  Hex_Digit_Display hex_digit_display_2 (.value(num[31:28]));  // open: dp
  // Probe on Instruct_ID
  // Probe on Instruct_EX
  // Probe on Instruct_Mem
  // Probe on Instruct_WB
  // Probe on ALU_result
  // Probe on Din
  // Probe on Next_PC
  not not_2 (not_2_out, and_1_out);
  and and_1 (and_1_out, clt13, equal2);
  Hex_Digit_Display hex_digit_display_3 (.value(num[19:16]));  // open: dp
  Hex_Digit_Display hex_digit_display_4 (.value(num[23:20]));  // open: dp
  ROM #(.addrWidth(10), .dataWidth(32)) rom_1 (.addr(register_1_q[11:2]), .data(rom_1_data), .sel(1'b1));
  Clock clock_1 (.out(clock_1_out));
  D_Flip_Flop d_ff_1 (.clk(not_2_out), .D(not_2_out), .Q(d_ff_1_q));  // open: Qn, preset, en, reset
  Hex_Digit_Display hex_digit_display_5 (.value(num[11:8]));  // open: dp
  Hex_Digit_Display hex_digit_display_6 (.value(num[15:12]));  // open: dp
  Bubble_Logic bubble_logic_1 (
    .I_ID(Instruct_ID), .I_EX(Instruct_EX), .I_Mem(Instruct_Mem), .I_WB(Instruct_WB), .out_5(ID_EX_RE),
    .out_6(ID_Mem_RE), .out_7(ID_WB_RE));
  IF_ID if_id_1 (
    .Instruction(rom_1_data), .PC(register_1_q[11:2]), ._PC_4(npc_1_out_5), .clk(clk), .WE(1'b1),
    .Instruction_out(Instruct_ID), ._PC_4_out(PC_4_ID), .clr(PC_Chged));  // open: PC_out
  or or_2 (clk, clock_1_out, d_ff_1_q);
  Hex_Digit_Display hex_digit_display_7 (.value(num[3:0]));  // open: dp
  Hex_Digit_Display hex_digit_display_8 (.value(num[7:4]));  // open: dp
  IR ir_1 (
    .in_1(Instruct_ID), .Rs_21_25(ir_1_rs_21_25), .Rt_16_20(ir_1_rt_16_20), .Rd_11_15(ir_1_rd_11_15),
    .Op_26_31(ir_1_op_26_31), .IM_0_15(ir_1_im_0_15), .funct_0_5(ir_1_funct_0_5));  // open: l26_0_25, shmat_6_10
  assign bit_extender_1_out = {{16{ir_1_im_0_15[15]}}, ir_1_im_0_15};  // Bit_Extender bit_extender_1
  Button INT1 (.out(INT1_out));
  Button INT2 (.out(INT2_out));
  Button INT3 (.out(INT3_out));
  // Probe on ir_1_op_26_31
  D_Flip_Flop d_ff_2 (
    .clk(INT1_out), .D(1'b1), .Q(d_ff_2_q), .en(1'b1), .reset(demultiplexer_1_out1));  // open: Qn, preset
  D_Flip_Flop d_ff_3 (
    .clk(INT2_out), .D(1'b1), .Q(d_ff_3_q), .en(1'b1), .reset(demultiplexer_1_out2));  // open: Qn, preset
  D_Flip_Flop d_ff_4 (
    .clk(INT3_out), .D(1'b1), .Q(d_ff_4_q), .en(1'b1), .reset(demultiplexer_1_out3));  // open: Qn, preset
  Multiplexer #(.width(5), .disabled(0), .enable("false")) multiplexer_2 (
    .in0(Rd_WB), .in1(Rt_WB), .out(multiplexer_2_out), .sel(or_3_out));
  Multiplexer #(.width(5), .disabled(0), .enable("false")) multiplexer_3 (
    .in0(multiplexer_2_out), .in1({5{1'b1}}), .out(multiplexer_3_out), .sel(clt11));
  or or_3 (or_3_out, clt9, clt18_ID);
  and and_2 (and_2_out, d_ff_2_q, IM1);
  and and_3 (and_3_out, d_ff_3_q, IM2);
  and and_4 (and_4_out, d_ff_4_q, IM3);
  Control control_1 (
    .in_1(ir_1_op_26_31), .ctl1(control_1_ctl1[0]), .ctl2(control_1_ctl1[1]), .ctl3(control_1_ctl1[2]),
    .ctl4(control_1_ctl1[3]), .ctl5(control_1_ctl1[4]), .ctl6(control_1_ctl1[5]), .ctl8(control_1_ctl1[6]),
    .ctl9(control_1_ctl1[7]), .ctl10(control_1_ctl1[8]), .ctl11(control_1_ctl1[9]), .op(clt7),
    .ctl14(control_1_ctl1[14]), .ctl15(control_1_ctl1[15]), .ctl16(control_1_ctl1[16]),
    .ctl17(control_1_ctl17), .ctl18(control_1_ctl18));
  // Probe on main_1_s0_value
  // Probe on multiplexer_3_out
  and and_5 (and_5_out, clt8, not_3_out);
  not not_3 (not_3_out, clt12_ID);
  or or_4 (or_4_out, clt19, INT);
  // Probe on multiplexer_13_out
  ctl18 ctl18_1 (
    .M5(ir_1_rs_21_25[4]), .M4(ir_1_rs_21_25[3]), .M3(ir_1_rs_21_25[2]), .M2(ir_1_rs_21_25[1]),
    .M1(ir_1_rs_21_25[0]), ._ctl18(control_1_ctl18), .ctl18(clt18_ID), .ctl19(clt19), .ctl20(clt20_ID));
  regfile2_main main_1 (
    .Reg1_num(ir_1_rs_21_25), .Reg2(ir_1_rt_16_20), .Write_Reg_num(multiplexer_3_out), .Din(Din),
    .Write_Enable(or_5_out), .Clock(clk), .Reg1(main_1_reg1), .Reg2_2(main_1_reg2_2),
    .s0_Value(main_1_s0_value), .s1_Value(main_1_s1_value));  // open: s2_Value, ra_Value
  // Probe on Din
  or or_5 (or_5_out, clt18_ID, and_5_out);
  not not_4 (IM1, cp0_1_im1);
  not not_5 (IM3, cp0_1_im3);
  not not_6 (IM2, cp0_1_im2);
  cp0 cp0_1 (
    .En(or_4_out), .INPUT(multiplexer_4_out), .EPC(cp0_1_epc), .OUTPUT(CP0_out), .IE(IE), .IM3(cp0_1_im3),
    .IM2(cp0_1_im2), .IM1(cp0_1_im1), .IN_SEL(multiplexer_13_out), .clk(not_7_out), .INT(INT),
    .ctl20(clt20_ID), .OUT_SEL(multiplexer_13_out));
  not not_7 (not_7_out, clk);
  // Probe on multiplexer_13_out
  Demultiplexer #(.select(2), .disabled(0), .enable("false")) demultiplexer_1 (
    .out1(demultiplexer_1_out1), .out2(demultiplexer_1_out2), .out3(demultiplexer_1_out3), .in(d_ff_5_q),
    .sel(out_6));  // open: out0
  ctl17 ctl17_1 (
    ._ctl17(control_1_ctl17), .B5(ir_1_rt_16_20[4]), .B4(ir_1_rt_16_20[3]), .B3(ir_1_rt_16_20[2]),
    .B2(ir_1_rt_16_20[1]), .B1(ir_1_rt_16_20[0]), .ctl17(control_1_ctl1[17]));
  Comparator #(.width(32)) comparator_1 (.a(main_1_s0_value), .b(32'ha), .eq(equal2));  // open: gt, lt
  not not_8 (not_8_out, equal2);
  // Probe on main_1_s1_value
  Priority_Encoder #(.select(2), .disabled(0)) priority_encoder_1 (
    .in0(1'b1), .in1(and_2_out), .in2(and_3_out), .in3(and_4_out), .out(out_6), .en_out(out_5), .en_in(1'b1));  // open: gs
  or or_6 (out_8, and_2_out, and_3_out, and_4_out);
  ALUctl aluctl_1 (
    .in_2(clt7), .in_1(ir_1_funct_0_5), .out_4(aluctl_1_out_4), .ctl12(clt12_ID), .ctl13(control_1_ctl1[22]),
    .ctl_sft(control_1_ctl1[23]));
  and and_6 (and_6_out, not_8_out, clt13);
  Multiplexer #(.width(32), .disabled(0), .enable("false")) multiplexer_4 (
    .in0(main_1_reg2_2), .in1(multiplexer_15_out), .out(multiplexer_4_out), .sel(INT));
  not not_9 (not_9_out, IE);
  Register #(.width(32)) register_2 (.D(main_1_s1_value), .en(and_6_out), .Q(num), .clk(clk), .clr(in_1));
  // Probe on main_1_reg2_2
  // Probe on ir_2_l26_0_25[27:2]
  // Probe on ir_2_l26_0_25[31:28]
  and and_7 (INT, out_8, IE);
  D_Flip_Flop d_ff_5 (.clk(not_9_out), .D(out_8), .Q(d_ff_5_q), .en(1'b1), .reset(IE));  // open: Qn, preset
  not not_10 (not_10_out, PC_Chged);
  and and_8 (and_8_out, not_10_out, No_relative);
  // Probe on Instruct_ID
  // Probe on Instruct_EX
  ID_EX id_ex_1 (
    .Sig({8'ha, control_1_ctl1[23:22], clt12_ID, clt20_ID, clt19, clt18_ID, control_1_ctl1[17:14], aluctl_1_out_4, control_1_ctl1[9:0]}),
    .R1(main_1_reg1), .R2(main_1_reg2_2), .Ext(bit_extender_1_out), .Instruction(Instruct_ID), .PC(PC_4_ID),
    .clk(clk), .WE(1'b1),
    .Sig_out({id_ex_1_sig_out[31:24], clt_sft, id_ex_1_sig_out[22], clt12_EX, clt20_EX, id_ex_1_sig_out[19:18], clt17, id_ex_1_sig_out[16], clt15, id_ex_1_sig_out[14], op, id_ex_1_sig_out[9], clt10, id_ex_1_sig_out[7:6], clt6, id_ex_1_sig_out[4:2], ctl2, ctl1}),
    .R1_out(R1), .R2_out(id_ex_1_r2_out), .Ext_out(Ext), .Instruction_out(Instruct_EX), .PC_out(PC_4_EX),
    .clr(and_9_out), .No_relative(and_8_out), .J(PC_Chged));
  and and_9 (and_9_out, Relative, not_11_out);
  not not_11 (not_11_out, clk);
  Multiplexer #(.width(32), .disabled(0), .enable("false")) multiplexer_5 (
    .in0(y1), .in1(shmat), .out(multiplexer_5_out), .sel(clt_sft));
  Shifter #(.width(32)) shifter_1 (.in(Ext), .\dist (5'b00010), .out(shifter_1_out));
  Adder #(.width(32)) adder_1 (.a(shifter_1_out), .b(PC_4_EX), .out(adder_1_out));  // open: cin, cout
  not not_12 (not_12_out, equal);
  Multiplexer #(.select(2), .width(32), .disabled(0), .enable("false")) multiplexer_6 (
    .in0({32{1'b0}}), .in1(32'h36c), .in2(32'h3e4), .in3(32'h45e), .out(INT_PC), .sel(out_6));
  // Probe on INT_PC
  Multiplexer #(.width(32), .disabled(0), .enable("false")) multiplexer_7 (
    .in0(R1), .in1(y1), .out(multiplexer_7_out), .sel(or_7_out));
  or or_7 (or_7_out, clt_sft, clt15);
  Multiplexer #(.width(32), .disabled(0), .enable("false")) multiplexer_8 (
    .in0(multiplexer_5_out), .in1(32'h10), .out(multiplexer_8_out), .sel(clt15));
  Multiplexer #(.disabled(0), .enable("false")) multiplexer_9 (
    .in0(equal), .in1(not_12_out), .out(multiplexer_9_out), .sel(clt10));
  Multiplexer #(.width(32), .disabled(0), .enable("false")) multiplexer_10 (
    .in0(id_ex_1_r2_out), .in1(Ext), .out(y1), .sel(clt6));
  // Probe on multiplexer_7_out
  ALU alu_1 (
    .AluOP(op), .X(multiplexer_7_out), .Equal(equal), .Result(ALU_result), .Y(multiplexer_11_out));  // open: Signed_Overflow, Result_2, UnSigned_Overflow
  Multiplexer #(.width(32), .disabled(0), .enable("false")) multiplexer_11 (
    .in0(multiplexer_8_out), .in1({32{1'b0}}), .out(multiplexer_11_out), .sel(clt17));
  // Probe on op
  // Probe on multiplexer_11_out
  Bit_Extender #(.in_width(5), .out_width(2)) bit_extender_2 (.in(ir_1_rd_11_15), .out(bit_extender_2_out));
  Multiplexer #(.width(32), .disabled(0), .enable("false")) multiplexer_12 (
    .in0(PC_4_EX), .in1(adder_1_out), .out(multiplexer_12_out), .sel(and_10_out));
  and and_10 (and_10_out, ctl1, multiplexer_9_out);
  // Probe on Instruct_EX
  Multiplexer #(.width(2), .disabled(0), .enable("false")) multiplexer_13 (
    .in0(bit_extender_2_out), .in1(2'b10), .out(multiplexer_13_out), .sel(INT));
  Multiplexer #(.width(32), .disabled(0), .enable("false")) multiplexer_14 (
    .in0(multiplexer_12_out), .in1({ir_2_l26_0_25, 2'b00}), .out(multiplexer_14_out), .sel(ctl2));
  Bit_Extender #(.in_width(32), .out_width(1)) bit_extender_3 (.in(ALU_result), .out(bit_extender_3_out));
  not not_13 (not_13_out, bit_extender_3_out);
  Multiplexer #(.width(32), .disabled(0), .enable("false")) multiplexer_15 (
    .in0(multiplexer_14_out), .in1(R1), .out(multiplexer_15_out), .sel(clt12_EX));
  or or_8 (or_8_out, equal, not_13_out);
  Multiplexer #(.width(32), .disabled(0), .enable("false")) multiplexer_16 (
    .in0(multiplexer_15_out), .in1(INT_PC), .out(multiplexer_16_out), .sel(INT));
  IR ir_2 (
    .in_1(Instruct_EX), .l26_0_25(ir_2_l26_0_25[27:2]), .shmat_6_10(ir_2_shmat_6_10));  // open: Rs_21_25, Rt_16_20, Rd_11_15, Op_26_31, IM_0_15, funct_0_5
  assign shmat = {{27{ir_2_shmat_6_10[4]}}, ir_2_shmat_6_10};  // Bit_Extender bit_extender_4
  and and_11 (BGEZ, clt17, or_8_out);
  Multiplexer #(.width(32), .disabled(0), .enable("false")) multiplexer_17 (
    .in0(multiplexer_16_out), .in1(cp0_1_epc), .out(PC_EX), .sel(clt20_EX));
  // Probe on PC_EX
  EX_Mem ex_mem_1 (
    .ALU_result(ALU_result), .zero(equal), .R2(id_ex_1_r2_out), .Instruction(Instruct_EX), .PC(PC_EX),
    .clk(clk), .WE(1'b1), .ALU_result_out(ex_mem_1_alu_result_out), .R2_out(ex_mem_1_r2_out),
    .Instruction_out(Instruct_Mem), .PC_out(PC_Mem),
    .Sig({id_ex_1_sig_out[31:24], clt_sft, id_ex_1_sig_out[22], clt12_EX, clt20_EX, id_ex_1_sig_out[19:18], clt17, id_ex_1_sig_out[16], clt15, id_ex_1_sig_out[14], op, id_ex_1_sig_out[9], clt10, id_ex_1_sig_out[7:6], clt6, id_ex_1_sig_out[4:2], ctl2, ctl1}),
    .Sig_out({ex_mem_1_sig_out[31:5], clt5, clt4, ex_mem_1_sig_out[2:0]}), .clr(1'b0),
    .PC_changed_EX(or_9_out), .PC_changed_Mem(PC_Chged), .PC_4_Current(PC_4_EX), .PC_4_c_out(PC_4_Mem));  // open: zero_out
  // Probe on Instruct_Mem
  or or_9 (or_9_out, and_10_out, ctl2, clt12_EX, INT, clt20_EX);
  RAM #(.addrWidth(10), .dataWidth(32), .bus("separate")) ram_1 (
    .addr(ex_mem_1_alu_result_out[11:2]), .din(ex_mem_1_r2_out), .data(ram_1_data), .str(clt5), .sel(1'b1),
    .clk(clk), .ld(clt4), .clr(in_3));
  Mem_WB mem_wb_1 (
    .byte_sel(ex_mem_1_alu_result_out[1:0]), .RD(ram_1_data), .ALU_Result(ex_mem_1_alu_result_out),
    .clk(clk), .WE(1'b1), .byte_sel_out(mem_wb_1_byte_sel_out), .RD_out(mem_wb_1_rd_out),
    .ALU_Result_out(mem_wb_1_alu_result_out),
    .Sig({ex_mem_1_sig_out[31:5], clt5, clt4, ex_mem_1_sig_out[2:0]}),
    .Sig_out({mem_wb_1_sig_out[31:23], clt13, mem_wb_1_sig_out[21:19], clt18_WB, mem_wb_1_sig_out[17], clt16, mem_wb_1_sig_out[15], clt14, mem_wb_1_sig_out[13:10], clt11, mem_wb_1_sig_out[8], clt9, clt8, mem_wb_1_sig_out[5:4], clt3, mem_wb_1_sig_out[2:0]}),
    .Instruction(Instruct_Mem), .Instruction_out(Instruct_WB), .clr(1'b0), .PC(PC_4_Mem), .PC_out(PC_4_WB));
  byte_selector byte_selector_1 (
    .data(mem_wb_1_rd_out), .selector(mem_wb_1_byte_sel_out), .out_3(byte_selector_1_out_3));
  assign bit_extender_5_out = {{24{1'b0}}, byte_selector_1_out_3};  // Bit_Extender bit_extender_5
  IR ir_3 (
    .in_1(Instruct_WB), .Rt_16_20(Rt_WB), .Rd_11_15(Rd_WB));  // open: Rs_21_25, Op_26_31, IM_0_15, l26_0_25, funct_0_5, shmat_6_10
  // Probe on Rd_WB
  Multiplexer #(.width(32), .disabled(0), .enable("false")) multiplexer_18 (
    .in0(mem_wb_1_rd_out), .in1(bit_extender_5_out), .out(multiplexer_18_out), .sel(clt16));
  Multiplexer #(.width(32), .disabled(0), .enable("false")) multiplexer_19 (
    .in0(mem_wb_1_alu_result_out), .in1(multiplexer_18_out), .out(multiplexer_19_out), .sel(clt3));
  Adder #(.width(32)) adder_2 (.a(PC_4_WB), .b(32'h4));  // open: out, cin, cout
  Multiplexer #(.width(32), .disabled(0), .enable("false")) multiplexer_20 (
    .in0(multiplexer_19_out), .in1(PC_4_WB), .out(multiplexer_20_out), .sel(clt14));
  // Probe on Din
  Multiplexer #(.width(32), .disabled(0), .enable("false")) multiplexer_21 (
    .in0(multiplexer_20_out), .in1(CP0_out), .out(Din), .sel(clt18_WB));

  assign out_7 = out_6;

  // Notes on the sheet:
  //   contents of rom_1 (hex, n*v repeats v):
  //   20110001 8100005 20110001 20120002 20130003 8100009 20110001 20120002 20130003 810000d 20110001
  //   20120002 20130003 8100011 20110001 20120002 20130003 c1000b8 20100001 20110001 118fc0 112020
  //   20020022 c 118882 12200001 8100015 112020 20020022 c 20110001 118880 112020 20020022 c 12200001
  //   810001f 20110001 118fc0 112020 20020022 c 1188c3 112020 20020022 c 118903 112020 20020022 c 118903
  //   112020 20020022 c 118903 112020 20020022 c 118903 112020 20020022 c 118903 112020 20020022 c 118903
  //   112020 20020022 c 118903 112020 20020022 c 20100001 109fc0 139fc3 8021 2012000c 24160003 26100001
  //   3210000f 20080008 20090001 139900 2709825 132020 20020022 c 1094022 1500fff9 22100001 2018000f
  //   2188024 108700 20080008 20090001 139902 2709825 132021 20020022 c 1094022 1500fff9 108702 2c9b022
  //   12c00001 8100050 4020 1084027 84400 3508ffff 82021 20020022 c 2010ffff 20110000 ae300000 22100001
  //   22310004 ae300000 22100001 22310004 ae300000 22100001 22310004 ae300000 22100001 22310004 ae300000
  //   22100001 22310004 ae300000 22100001 22310004 ae300000 22100001 22310004 ae300000 22100001 22310004
  //   ae300000 22100001 22310004 ae300000 22100001 22310004 ae300000 22100001 22310004 ae300000 22100001
  //   22310004 ae300000 22100001 22310004 ae300000 22100001 22310004 ae300000 22100001 22310004 ae300000
  //   22100001 22310004 22100001 8020 2011003c 8e130000 8e340000 274402a 11000002 ae330000 ae140000
  //   2231fffc 1611fff8 102020 20020022 c 22100004 2011003c 1611fff2 2002000a c 20100000 22100001 102020
  //   20020022 c 22100002 102020 20020022 c 22100003 102020 20020022 c 22100004 102020 20020022 c 22100005
  //   102020 20020022 c 22100006 102020 20020022 c 22100007 102020 20020022 c 22100008 102020 20020022
  //   20020022 c 3e00008
endmodule

module IR (
  input  [31:0] in_1,
  output [5:0] Op_26_31,
  output [4:0] Rs_21_25,
  output [4:0] Rt_16_20,
  output [4:0] Rd_11_15,
  output [4:0] shmat_6_10,
  output [15:0] IM_0_15,
  output [25:0] l26_0_25,
  output [5:0] funct_0_5
);


  assign funct_0_5 = in_1[5:0];
  assign IM_0_15 = in_1[15:0];
  assign l26_0_25 = in_1[25:0];
  assign Op_26_31 = in_1[31:26];
  assign Rd_11_15 = in_1[15:11];
  assign Rs_21_25 = in_1[25:21];
  assign Rt_16_20 = in_1[20:16];
  assign shmat_6_10 = in_1[10:6];
endmodule

module Control (
  input  [5:0] in_1,
  output ctl1,
  output ctl2,
  output ctl3,
  output ctl4,
  output ctl5,
  output ctl6,
  output ctl8,
  output ctl9,
  output ctl10,
  output ctl11,
  output ctl14,
  output ctl15,
  output [3:0] op,
  output ctl16,
  output ctl17,
  output ctl18
);

  ctl ctl_1 (
    .op31(in_1[5]), .ctl1(ctl1), .op30(in_1[4]), .ctl2(ctl2), .op29(in_1[3]), .ctl3(ctl3), .op28(in_1[2]),
    .ctl4(ctl4), .op27(in_1[1]), .ctl5(ctl5), .op26(in_1[0]), .ctl6(ctl6), .ctl8(ctl8), .ctl9(ctl9),
    .ctl10(ctl10), .ctl11(ctl11), .ctl14(ctl14), .ctl15(ctl15));
  opctl opctl_1 (
    .op31(in_1[5]), .op30(in_1[4]), .op29(in_1[3]), .op28(in_1[2]), .op27(in_1[1]), .op26(in_1[0]),
    .op4(op[3]), .op3(op[2]), .op2(op[1]), .op1(op[0]));
  ctl2 ctl2_1 (
    .op31(in_1[5]), .op30(in_1[4]), .op29(in_1[3]), .op28(in_1[2]), .op27(in_1[1]), .op26(in_1[0]),
    .ctl16(ctl16), .ctl17(ctl17), .ctl18(ctl18));
endmodule

module NPC (
  input  [31:0] PC,
  input  [15:0] IM,
  input  BGEZ,
  output [31:0] jia8,
  output [31:0] out_5,
  output [3:0] high4
);

  wire [31:0] bit_extender_1_out, multiplexer_1_out, shifter_1_out;

  assign bit_extender_1_out = {{16{1'b0}}, IM};  // Bit_Extender bit_extender_1
  Shifter #(.width(32)) shifter_1 (.in(bit_extender_1_out), .\dist (5'b00010), .out(shifter_1_out));
  Adder #(.width(32)) adder_1 (.a(PC), .b(multiplexer_1_out), .out({high4, out_5[27:0]}));  // open: cin, cout
  Multiplexer #(.width(32), .disabled(0), .enable("false")) multiplexer_1 (
    .in0(32'h4), .in1(shifter_1_out), .out(multiplexer_1_out), .sel(BGEZ));
  Adder #(.width(32)) adder_2 (.a(PC), .b(32'h8), .out(jia8));  // open: cin, cout

  assign out_5[31:28] = high4;
endmodule

module ALUctl (
  input  [5:0] in_1,
  input  [3:0] in_2,
  output ctl13,
  output [3:0] out_4,
  output ctl12,
  output ctl_sft
);

  wire and_1_out, and_2_out, and_3_out, and_6_out, ctl_sft_1_ctl_sft, not_1_out, not_2_out, not_3_out,
       not_4_out, not_5_out, not_6_out, not_7_out, not_8_out, not_9_out;
  wire [3:0] ac_1_op1;

  ctl_sft ctl_sft_1 (
    .f6(in_1[5]), .f5(in_1[4]), .f4(in_1[3]), .f3(in_1[2]), .f2(in_1[1]), .f1(in_1[0]),
    .ctl_sft(ctl_sft_1_ctl_sft));
  not not_1 (not_1_out, in_1[0]);
  not not_2 (not_2_out, in_1[1]);
  not not_3 (not_3_out, in_1[2]);
  not not_4 (not_4_out, in_1[4]);
  not not_5 (not_5_out, in_1[5]);
  ac ac_1 (
    .f6(in_1[5]), .op4(ac_1_op1[3]), .f5(in_1[4]), .f4(in_1[3]), .op3(ac_1_op1[2]), .f3(in_1[2]),
    .f2(in_1[1]), .f1(in_1[0]), .op2(ac_1_op1[1]), .op1(ac_1_op1[0]));
  and and_1 (and_1_out, not_1_out, not_2_out, not_3_out, in_1[3], not_4_out);
  and and_2 (and_2_out, and_1_out, not_5_out);
  Multiplexer #(.width(4), .disabled(0), .enable("false")) multiplexer_1 (
    .in0(in_2), .in1(ac_1_op1), .out(out_4), .sel(and_3_out));
  and and_3 (and_3_out, in_2[0], in_2[1], in_2[2], in_2[3]);
  and and_4 (ctl_sft, and_3_out, ctl_sft_1_ctl_sft);
  and and_5 (ctl12, and_3_out, and_2_out);
  not not_6 (not_6_out, in_1[0]);
  not not_7 (not_7_out, in_1[1]);
  and and_6 (and_6_out, not_6_out, not_7_out, in_1[2], not_8_out, not_9_out, in_1[3]);
  not not_8 (not_8_out, in_1[4]);
  not not_9 (not_9_out, in_1[5]);
  and and_7 (ctl13, and_6_out, and_3_out);
endmodule

module ctl (
  input  op31,
  input  op30,
  input  op29,
  input  op28,
  input  op27,
  input  op26,
  output ctl1,
  output ctl2,
  output ctl3,
  output ctl4,
  output ctl5,
  output ctl6,
  output ctl8,
  output ctl9,
  output ctl10,
  output ctl11,
  output ctl14,
  output ctl15
);

  wire and_6_out, and_7_out, and_8_out, and_9_out, and_10_out, and_11_out, and_12_out, and_13_out,
       and_14_out, and_15_out, and_16_out, and_17_out, and_18_out, not_1_out, not_2_out, not_3_out,
       not_4_out, not_5_out, not_6_out, not_7_out, not_8_out, not_9_out, not_10_out, not_11_out, not_12_out,
       not_13_out, not_14_out, not_15_out, not_16_out, not_17_out, not_18_out, not_19_out, not_20_out,
       not_21_out, not_22_out, not_23_out, not_24_out, not_25_out, not_26_out, not_27_out, not_28_out,
       not_29_out, not_30_out, not_31_out, not_32_out, not_33_out, not_34_out, not_35_out;

  not not_1 (not_1_out, op29);
  not not_2 (not_2_out, op31);
  not not_3 (not_3_out, op29);
  not not_4 (not_4_out, op29);
  not not_5 (not_5_out, op29);
  and and_1 (ctl5, op31, op29);
  or or_1 (ctl6, op29, op31);
  not not_6 (not_6_out, op30);
  not not_7 (not_7_out, op28);
  not not_8 (not_8_out, op27);
  not not_9 (not_9_out, op26);
  not not_10 (not_10_out, op30);
  not not_11 (not_11_out, op29);
  not not_12 (not_12_out, op28);
  not not_13 (not_13_out, op31);
  not not_14 (not_14_out, op28);
  not not_15 (not_15_out, op27);
  not not_16 (not_16_out, op29);
  not not_17 (not_17_out, op28);
  not not_18 (not_18_out, op27);
  not not_19 (not_19_out, op31);
  not not_20 (not_20_out, op29);
  not not_21 (not_21_out, op29);
  not not_22 (not_22_out, op27);
  not not_23 (not_23_out, op29);
  not not_24 (not_24_out, op27);
  not not_25 (not_25_out, op31);
  not not_26 (not_26_out, op29);
  not not_27 (not_27_out, op31);
  not not_28 (not_28_out, op28);
  not not_29 (not_29_out, op31);
  not not_30 (not_30_out, op31);
  not not_31 (not_31_out, op30);
  not not_32 (not_32_out, op29);
  not not_33 (not_33_out, op28);
  not not_34 (not_34_out, op31);
  not not_35 (not_35_out, op30);
  and and_2 (ctl1, not_1_out, op28);
  and and_3 (ctl2, not_2_out, not_3_out, op27);
  and and_4 (ctl3, op31, not_4_out);
  and and_5 (ctl4, op31, not_5_out);
  and and_6 (and_6_out, not_6_out, not_7_out, not_8_out, not_9_out);
  and and_7 (and_7_out, not_10_out, not_11_out, not_12_out, op27, op26);
  and and_8 (and_8_out, not_13_out, op29);
  and and_9 (and_9_out, op30, not_14_out, not_15_out, op26);
  and and_10 (and_10_out, op31, not_16_out);
  and and_11 (and_11_out, op31, not_17_out, not_18_out);
  and and_12 (and_12_out, not_19_out, op29);
  and and_13 (and_13_out, op31, not_20_out);
  and and_14 (and_14_out, not_21_out, op28, not_22_out, op26);
  and and_15 (and_15_out, op30, not_23_out, not_24_out, op26);
  and and_16 (and_16_out, not_25_out, not_26_out, op27, op26);
  and and_17 (and_17_out, not_27_out, not_28_out, op27, op26);
  and and_18 (and_18_out, not_29_out, op30, op27, op26);
  and and_19 (ctl14, not_30_out, not_31_out, not_32_out, not_33_out, op27, op26);
  and and_20 (ctl15, not_34_out, not_35_out, op29, op28, op27, op26);
  or or_2 (ctl8, and_6_out, and_7_out, and_8_out, and_9_out, and_10_out, and_11_out);
  or or_3 (ctl9, and_12_out, and_13_out);
  or or_4 (ctl10, and_14_out, and_15_out);
  or or_5 (ctl11, and_16_out, and_17_out, and_18_out);
endmodule

module ctl2 (
  input  op31,
  input  op30,
  input  op29,
  input  op28,
  input  op27,
  input  op26,
  output ctl16,
  output ctl17,
  output ctl18
);

  wire not_1_out, not_2_out, not_3_out, not_4_out, not_5_out, not_6_out, not_7_out, not_8_out, not_9_out,
       not_10_out, not_11_out, not_12_out, not_13_out, not_14_out;

  not not_1 (not_1_out, op30);
  not not_2 (not_2_out, op29);
  not not_3 (not_3_out, op28);
  not not_4 (not_4_out, op27);
  not not_5 (not_5_out, op31);
  not not_6 (not_6_out, op30);
  not not_7 (not_7_out, op29);
  not not_8 (not_8_out, op28);
  not not_9 (not_9_out, op27);
  not not_10 (not_10_out, op31);
  not not_11 (not_11_out, op29);
  not not_12 (not_12_out, op28);
  not not_13 (not_13_out, op27);
  not not_14 (not_14_out, op26);
  and and_1 (ctl16, op31, not_1_out, not_2_out, not_3_out, not_4_out, op26);
  and and_2 (ctl17, not_5_out, not_6_out, not_7_out, not_8_out, not_9_out, op26);
  and and_3 (ctl18, not_10_out, op30, not_11_out, not_12_out, not_13_out, not_14_out);
endmodule

module ac (
  input  f6,
  input  f5,
  input  f4,
  input  f3,
  input  f2,
  input  f1,
  output op4,
  output op3,
  output op2,
  output op1
);

  wire and_1_out, and_2_out, and_3_out, and_4_out, and_5_out, and_6_out, and_7_out, and_8_out, and_9_out,
       and_10_out, not_1_out, not_2_out, not_3_out, not_4_out, not_5_out, not_6_out, not_7_out, not_8_out,
       not_9_out, not_10_out;

  and and_1 (and_1_out, f3, f1);
  not not_1 (not_1_out, f1);
  not not_2 (not_2_out, f4);
  not not_3 (not_3_out, f3);
  not not_4 (not_4_out, f1);
  not not_5 (not_5_out, f1);
  not not_6 (not_6_out, f4);
  not not_7 (not_7_out, f3);
  not not_8 (not_8_out, f1);
  not not_9 (not_9_out, f2);
  not not_10 (not_10_out, f1);
  or or_1 (op4, and_1_out, f4);
  and and_2 (and_2_out, f3, not_1_out);
  and and_3 (and_3_out, f4, f1);
  and and_4 (and_4_out, f6, not_2_out, not_3_out);
  and and_5 (and_5_out, f2, not_4_out);
  and and_6 (and_6_out, f3, not_5_out);
  and and_7 (and_7_out, not_6_out, not_7_out, f1);
  and and_8 (and_8_out, f3, f2);
  and and_9 (and_9_out, f4, not_8_out);
  and and_10 (and_10_out, f6, not_9_out, not_10_out);
  or or_2 (op3, and_2_out, and_3_out, and_4_out);
  or or_3 (op2, and_5_out, and_6_out);
  or or_4 (op1, and_7_out, and_8_out, and_9_out, and_10_out);
endmodule

module opctl (
  input  op31,
  input  op30,
  input  op29,
  input  op28,
  input  op27,
  input  op26,
  output op4,
  output op3,
  output op2,
  output op1
);

  wire and_1_out, and_2_out, and_3_out, and_4_out, and_5_out, and_6_out, and_7_out, and_8_out, and_9_out,
       and_10_out, and_11_out, and_12_out, and_13_out, and_14_out, and_15_out, and_16_out, and_17_out,
       and_18_out, and_19_out, and_20_out, and_21_out, and_22_out, and_23_out, and_24_out, and_25_out,
       and_26_out, not_1_out, not_2_out, not_3_out, not_4_out, not_5_out, not_6_out, not_7_out, not_8_out,
       not_9_out, not_10_out, not_11_out, not_12_out, not_13_out, not_14_out, not_15_out, not_16_out,
       not_17_out, not_18_out, not_19_out, not_20_out, not_21_out, not_22_out, not_23_out, not_24_out,
       not_25_out, not_26_out, not_27_out, not_28_out, not_29_out, not_30_out, not_31_out, not_32_out,
       not_33_out, not_34_out, not_35_out, not_36_out, not_37_out, not_38_out, not_39_out, not_40_out,
       not_41_out, not_42_out, not_43_out, not_44_out, not_45_out, not_46_out, not_47_out, not_48_out,
       not_49_out, not_50_out, not_51_out, not_52_out, not_53_out, not_54_out, not_55_out, not_56_out;

  not not_1 (not_1_out, op31);
  not not_2 (not_2_out, op29);
  not not_3 (not_3_out, op28);
  not not_4 (not_4_out, op27);
  not not_5 (not_5_out, op29);
  not not_6 (not_6_out, op28);
  not not_7 (not_7_out, op27);
  not not_8 (not_8_out, op26);
  not not_9 (not_9_out, op26);
  not not_10 (not_10_out, op27);
  not not_11 (not_11_out, op29);
  not not_12 (not_12_out, op28);
  not not_13 (not_13_out, op27);
  not not_14 (not_14_out, op31);
  not not_15 (not_15_out, op30);
  not not_16 (not_16_out, op28);
  not not_17 (not_17_out, op27);
  not not_18 (not_18_out, op31);
  not not_19 (not_19_out, op30);
  not not_20 (not_20_out, op27);
  not not_21 (not_21_out, op26);
  not not_22 (not_22_out, op28);
  not not_23 (not_23_out, op28);
  not not_24 (not_24_out, op30);
  not not_25 (not_25_out, op28);
  not not_26 (not_26_out, op28);
  not not_27 (not_27_out, op31);
  not not_28 (not_28_out, op29);
  not not_29 (not_29_out, op28);
  not not_30 (not_30_out, op27);
  not not_31 (not_31_out, op29);
  not not_32 (not_32_out, op28);
  not not_33 (not_33_out, op27);
  not not_34 (not_34_out, op26);
  not not_35 (not_35_out, op31);
  not not_36 (not_36_out, op30);
  not not_37 (not_37_out, op28);
  not not_38 (not_38_out, op26);
  not not_39 (not_39_out, op31);
  not not_40 (not_40_out, op30);
  not not_41 (not_41_out, op27);
  not not_42 (not_42_out, op26);
  not not_43 (not_43_out, op29);
  not not_44 (not_44_out, op28);
  not not_45 (not_45_out, op27);
  not not_46 (not_46_out, op28);
  not not_47 (not_47_out, op27);
  not not_48 (not_48_out, op31);
  not not_49 (not_49_out, op30);
  not not_50 (not_50_out, op26);
  not not_51 (not_51_out, op31);
  not not_52 (not_52_out, op27);
  not not_53 (not_53_out, op26);
  not not_54 (not_54_out, op28);
  not not_55 (not_55_out, op30);
  not not_56 (not_56_out, op28);
  and and_1 (and_1_out, not_1_out, not_2_out, not_3_out, not_4_out);
  and and_2 (and_2_out, not_5_out, not_6_out, not_7_out, not_8_out);
  and and_3 (and_3_out, op29, op27, not_9_out);
  and and_4 (and_4_out, op29, op28, not_10_out, op26);
  and and_5 (and_5_out, op30, not_11_out, not_12_out, not_13_out);
  and and_6 (and_6_out, not_14_out, op30, op29, op28);
  and and_7 (and_7_out, op31, not_15_out, op29, op28);
  and and_8 (and_8_out, op31, op29, op28, op27);
  and and_9 (and_9_out, not_16_out, not_17_out);
  and and_10 (and_10_out, not_18_out, not_19_out, op29, not_20_out, not_21_out);
  and and_11 (and_11_out, op29, not_22_out, op26);
  and and_12 (and_12_out, op30, op29, not_23_out);
  and and_13 (and_13_out, op31, not_24_out, not_25_out, op26);
  and and_14 (and_14_out, op31, op29, not_26_out);
  and and_15 (and_15_out, not_27_out, not_28_out, not_29_out, not_30_out);
  and and_16 (and_16_out, not_31_out, not_32_out, not_33_out, not_34_out);
  and and_17 (and_17_out, not_35_out, not_36_out, op29, not_37_out, op27, not_38_out);
  and and_18 (and_18_out, not_39_out, not_40_out, op29, op28, not_41_out, not_42_out);
  and and_19 (and_19_out, op30, not_43_out, not_44_out, not_45_out);
  and and_20 (and_20_out, not_46_out, not_47_out);
  and and_21 (and_21_out, not_48_out, not_49_out, op29, not_50_out);
  and and_22 (and_22_out, not_51_out, op29, not_52_out, not_53_out);
  and and_23 (and_23_out, op29, not_54_out, op26);
  and and_24 (and_24_out, op30, op29, op26);
  and and_25 (and_25_out, op31, not_55_out, not_56_out, op26);
  and and_26 (and_26_out, op31, op29, op26);
  or or_1 (op4, and_1_out, and_2_out, and_3_out, and_4_out, and_5_out, and_6_out, and_7_out, and_8_out);
  or or_2 (op3, and_9_out, and_10_out, and_11_out, and_12_out, and_13_out, and_14_out);
  or or_3 (op2, and_15_out, and_16_out, and_17_out, and_18_out, and_19_out);
  or or_4 (op1, and_20_out, and_21_out, and_22_out, and_23_out, and_24_out, and_25_out, and_26_out);
endmodule

module ctl_sft (
  input  f6,
  input  f5,
  input  f4,
  input  f3,
  input  f2,
  input  f1,
  output ctl_sft
);

  wire and_1_out, and_2_out, not_1_out, not_2_out, not_3_out, not_4_out, not_5_out, not_6_out, not_7_out,
       not_8_out, not_9_out;

  not not_1 (not_1_out, f6);
  not not_2 (not_2_out, f5);
  not not_3 (not_3_out, f4);
  not not_4 (not_4_out, f3);
  not not_5 (not_5_out, f1);
  not not_6 (not_6_out, f6);
  not not_7 (not_7_out, f5);
  not not_8 (not_8_out, f4);
  not not_9 (not_9_out, f3);
  and and_1 (and_1_out, not_1_out, not_2_out, not_3_out, not_4_out, not_5_out);
  and and_2 (and_2_out, not_6_out, not_7_out, not_8_out, not_9_out, f2);
  or or_1 (ctl_sft, and_1_out, and_2_out);
endmodule

module byte_selector (
  input  [31:0] data,
  input  [1:0] selector,
  output [7:0] out_3
);

  Multiplexer #(.select(2), .width(8), .disabled(0), .enable("false")) multiplexer_1 (
    .in0(data[31:24]), .in1(data[23:16]), .in2(data[15:8]), .in3(data[7:0]), .out(out_3), .sel(selector));
endmodule

module ctl17 (
  input  _ctl17,
  input  B5,
  input  B4,
  input  B3,
  input  B2,
  input  B1,
  output ctl17
);

  wire not_1_out, not_2_out, not_3_out, not_4_out;

  not not_1 (not_1_out, B5);
  not not_2 (not_2_out, B4);
  not not_3 (not_3_out, B3);
  not not_4 (not_4_out, B2);
  and and_1 (ctl17, _ctl17, not_1_out, not_2_out, not_3_out, not_4_out, B1);
endmodule

module ctl18 (
  input  M5,
  input  M4,
  input  M3,
  input  M2,
  input  M1,
  input  _ctl18,
  output ctl18,
  output ctl19,
  output ctl20
);

  wire not_1_out, not_2_out, not_3_out, not_4_out, not_5_out, not_6_out, not_7_out, not_8_out, not_9_out,
       not_10_out, not_11_out, not_12_out, not_13_out;

  not not_1 (not_1_out, M5);
  not not_2 (not_2_out, M4);
  not not_3 (not_3_out, M3);
  not not_4 (not_4_out, M2);
  not not_5 (not_5_out, M1);
  not not_6 (not_6_out, M5);
  not not_7 (not_7_out, M4);
  not not_8 (not_8_out, M2);
  not not_9 (not_9_out, M1);
  not not_10 (not_10_out, M4);
  not not_11 (not_11_out, M3);
  not not_12 (not_12_out, M2);
  not not_13 (not_13_out, M1);
  and and_1 (ctl18, not_1_out, not_2_out, not_3_out, not_4_out, not_5_out, _ctl18);
  and and_2 (ctl19, not_6_out, not_7_out, M3, not_8_out, not_9_out, _ctl18);
  and and_3 (ctl20, M5, not_10_out, not_11_out, not_12_out, not_13_out, _ctl18);
endmodule

module cp0 (
  input  En,
  input  [1:0] OUT_SEL,
  input  [1:0] IN_SEL,
  input  clk,
  input  [31:0] INPUT,
  input  INT,
  input  ctl20,
  output IM3,
  output IM2,
  output IM1,
  output [31:0] EPC,
  output [31:0] OUTPUT,
  output IE
);

  wire bit_extender_1_out, demultiplexer_1_out0, demultiplexer_1_out1, demultiplexer_1_out2, or_1_out;
  wire [31:0] multiplexer_1_out, multiplexer_2_out, nIE_q;
  wire [31:3] INM_q;

  Demultiplexer #(.select(2), .disabled(0), .enable("false")) demultiplexer_1 (
    .out0(demultiplexer_1_out0), .out1(demultiplexer_1_out1), .out2(demultiplexer_1_out2), .in(En),
    .sel(IN_SEL));  // open: out3
  Register #(.width(32)) INM (.D(INPUT), .en(demultiplexer_1_out0), .Q({INM_q, IM3, IM2, IM1}), .clk(clk), .clr(1'b0));
  Register #(.width(32)) u_EPC (.D(INPUT), .en(demultiplexer_1_out2), .Q(EPC), .clk(clk), .clr(1'b0));
  Multiplexer #(.width(32), .disabled(0), .enable("false")) multiplexer_1 (
    .in0(INPUT), .in1(32'h1), .out(multiplexer_1_out), .sel(INT));
  Register #(.width(32)) nIE (.D(multiplexer_2_out), .en(or_1_out), .Q(nIE_q), .clk(clk), .clr(1'b0));
  or or_1 (or_1_out, demultiplexer_1_out1, ctl20, INT);
  Multiplexer #(.width(32), .disabled(0), .enable("false")) multiplexer_2 (
    .in0(multiplexer_1_out), .in1({32{1'b0}}), .out(multiplexer_2_out), .sel(ctl20));
  Bit_Extender #(.in_width(32), .out_width(1)) bit_extender_1 (.in(nIE_q), .out(bit_extender_1_out));
  Multiplexer #(.select(2), .width(32), .disabled(0), .enable("false")) multiplexer_3 (
    .in0({INM_q, IM3, IM2, IM1}), .in1(nIE_q), .in2(EPC), .out(OUTPUT), .sel(OUT_SEL));  // open: in3
  not not_1 (IE, bit_extender_1_out);
endmodule

module comp (
  input  [1:0] doing,
  input  [1:0] require,
  output out_3,
  output out_4,
  output out_5,
  output [1:0] out_6
);

  wire comparator_4_gt;

  Comparator #(.width(2)) comparator_1 (.a(2'b11), .b(doing), .gt(out_3));  // open: eq, lt
  Comparator #(.width(2)) comparator_2 (.a(2'b10), .b(doing), .gt(out_4));  // open: eq, lt
  Comparator #(.width(2)) comparator_3 (.a(2'b01), .b(doing), .gt(out_5));  // open: eq, lt
  Comparator #(.width(2)) comparator_4 (.a(doing), .b(require), .gt(comparator_4_gt));  // open: eq, lt
  Multiplexer #(.width(2), .disabled(0), .enable("false")) multiplexer_1 (
    .in0(doing), .in1(require), .out(out_6), .sel(comparator_4_gt));
endmodule

module INM (
  input  num1,
  input  num0,
  output INM1,
  output INM2,
  output INM3
);

  wire not_1_out, not_2_out, not_4_out, not_5_out;

  not not_1 (not_1_out, num1);
  not not_2 (not_2_out, num0);
  not not_3 (INM2, num1);
  not not_4 (not_4_out, num1);
  not not_5 (not_5_out, num0);
  and and_1 (INM1, not_1_out, not_2_out);
  or or_1 (INM3, not_4_out, not_5_out);
endmodule

module IF_ID (
  input  [31:0] Instruction,
  input  [9:0] PC,
  input  [31:0] _PC_4,
  input  clk,
  input  WE,
  input  clr,
  output [31:0] Instruction_out,
  output [9:0] PC_out,
  output [31:0] _PC_4_out
);

  wire d_ff_1_q;

  D_Flip_Flop d_ff_1 (.clk(clr), .D(1'b1), .Q(d_ff_1_q), .reset(clr));  // open: Qn, preset, en
  Register #(.width(32)) register_1 (.D(Instruction), .en(WE), .Q(Instruction_out), .clk(clk), .clr(d_ff_1_q));
  Register #(.width(10)) register_2 (.D(PC), .en(WE), .Q(PC_out), .clk(clk), .clr(d_ff_1_q));
  Register #(.width(32)) register_3 (.D(_PC_4), .en(WE), .Q(_PC_4_out), .clk(clk), .clr(d_ff_1_q));
endmodule

module ID_EX (
  input  [31:0] Sig,
  input  [31:0] R1,
  input  [31:0] R2,
  input  [31:0] Ext,
  input  [31:0] Instruction,
  input  [31:0] PC,
  input  clk,
  input  WE,
  input  No_relative,
  input  J,
  input  clr,
  output [31:0] Sig_out,
  output [31:0] R1_out,
  output [31:0] R2_out,
  output [31:0] Ext_out,
  output [31:0] Instruction_out,
  output [31:0] PC_out
);

  wire d_ff_1_q, d_ff_2_q, or_1_out;

  Register #(.width(32)) register_1 (.D(Sig), .en(WE), .Q(Sig_out), .clk(clk), .clr(or_1_out));
  Register #(.width(32)) register_2 (.D(R1), .en(WE), .Q(R1_out), .clk(clk), .clr(or_1_out));
  Register #(.width(32)) register_3 (.D(R2), .en(WE), .Q(R2_out), .clk(clk), .clr(or_1_out));
  Register #(.width(32)) register_4 (.D(Ext), .en(WE), .Q(Ext_out), .clk(clk), .clr(or_1_out));
  Register #(.width(32)) register_5 (.D(Instruction), .en(WE), .Q(Instruction_out), .clk(clk), .clr(or_1_out));
  Register #(.width(32)) register_6 (.D(PC), .en(WE), .Q(PC_out), .clk(clk), .clr(or_1_out));
  D_Flip_Flop d_ff_1 (.clk(clr), .D(clr), .Q(d_ff_1_q));  // open: Qn, preset, en, reset
  D_Flip_Flop d_ff_2 (.clk(clk), .D(d_ff_1_q), .Q(d_ff_2_q), .reset(No_relative));  // open: Qn, preset, en
  or or_1 (or_1_out, d_ff_2_q, J);
endmodule

module EX_Mem (
  input  PC_changed_EX,
  input  [31:0] Sig,
  input  [31:0] ALU_result,
  input  zero,
  input  [31:0] R2,
  input  [31:0] PC_4_Current,
  input  [31:0] Instruction,
  input  [31:0] PC,
  input  clk,
  input  WE,
  input  clr,
  output PC_changed_Mem,
  output [31:0] Sig_out,
  output [31:0] ALU_result_out,
  output zero_out,
  output [31:0] R2_out,
  output [31:0] PC_4_c_out,
  output [31:0] Instruction_out,
  output [31:0] PC_out
);

  wire d_ff_1_q, d_ff_2_q, not_1_out;

  Register #(.width(1)) register_1 (.D(PC_changed_EX), .en(WE), .Q(PC_changed_Mem), .clk(clk), .clr(d_ff_2_q));
  Register #(.width(32)) register_2 (.D(Sig), .en(WE), .Q(Sig_out), .clk(clk), .clr(d_ff_2_q));
  Register #(.width(32)) register_3 (.D(ALU_result), .en(WE), .Q(ALU_result_out), .clk(clk), .clr(d_ff_2_q));
  Register #(.width(1)) register_4 (.D(zero), .en(WE), .Q(zero_out), .clk(clk), .clr(d_ff_2_q));
  Register #(.width(32)) register_5 (.D(R2), .en(WE), .Q(R2_out), .clk(clk), .clr(d_ff_2_q));
  Register #(.width(32)) register_6 (.D(PC_4_Current), .en(WE), .Q(PC_4_c_out), .clk(clk), .clr(d_ff_2_q));
  Register #(.width(32)) register_7 (.D(Instruction), .en(WE), .Q(Instruction_out), .clk(clk), .clr(d_ff_2_q));
  Register #(.width(32)) register_8 (.D(PC), .en(WE), .Q(PC_out), .clk(clk), .clr(d_ff_2_q));
  D_Flip_Flop d_ff_1 (.clk(clr), .D(clr), .Q(d_ff_1_q));  // open: Qn, preset, en, reset
  not not_1 (not_1_out, clk);
  D_Flip_Flop d_ff_2 (.clk(clk), .D(d_ff_1_q), .Q(d_ff_2_q), .reset(not_1_out));  // open: Qn, preset, en
endmodule

module Mem_WB (
  input  [31:0] Instruction,
  input  [31:0] Sig,
  input  [1:0] byte_sel,
  input  [31:0] RD,
  input  [31:0] PC,
  input  [31:0] ALU_Result,
  input  clk,
  input  WE,
  input  clr,
  output [31:0] Instruction_out,
  output [31:0] Sig_out,
  output [1:0] byte_sel_out,
  output [31:0] RD_out,
  output [31:0] PC_out,
  output [31:0] ALU_Result_out
);

  wire d_ff_1_q, d_ff_2_q, not_1_out;

  Register #(.width(32)) register_1 (.D(Instruction), .en(WE), .Q(Instruction_out), .clk(clk), .clr(d_ff_2_q));
  Register #(.width(32)) register_2 (.D(Sig), .en(WE), .Q(Sig_out), .clk(clk), .clr(d_ff_2_q));
  Register #(.width(2)) register_3 (.D(byte_sel), .en(WE), .Q(byte_sel_out), .clk(clk), .clr(d_ff_2_q));
  Register #(.width(32)) register_4 (.D(RD), .en(WE), .Q(RD_out), .clk(clk), .clr(d_ff_2_q));
  Register #(.width(32)) register_5 (.D(PC), .en(WE), .Q(PC_out), .clk(clk), .clr(d_ff_2_q));
  Register #(.width(32)) register_6 (.D(ALU_Result), .en(WE), .Q(ALU_Result_out), .clk(clk), .clr(d_ff_2_q));
  D_Flip_Flop d_ff_1 (.clk(clr), .D(clr), .Q(d_ff_1_q));  // open: Qn, preset, en, reset
  not not_1 (not_1_out, clk);
  D_Flip_Flop d_ff_2 (.clk(clk), .D(d_ff_1_q), .Q(d_ff_2_q), .reset(not_1_out));  // open: Qn, preset, en
endmodule

module Bubble_Logic (
  input  [31:0] I_ID,
  input  [31:0] I_EX,
  input  [31:0] I_Mem,
  input  [31:0] I_WB,
  output out_5,
  output out_6,
  output out_7
);

  wire EX_nop, EX_sys, Mem_nop, Mem_sys, or_1_out, or_2_out, or_3_out, or_4_out, or_5_out, or_6_out,
       or_7_out, or_8_out, or_9_out, R_nop, R_sys, read_reg_1_rd_w, read_reg_1_rt_w, read_reg_2_rd_w,
       read_reg_2_rt_w, read_reg_3_rd_w, read_reg_3_rt_w, Rs_R, Rt_R, WB_nop, WB_sys;
  wire [4:0] ir_1_rs_21_25, ir_1_rt_16_20, ir_2_rd_11_15, ir_2_rt_16_20, ir_3_rd_11_15, ir_3_rt_16_20,
       ir_4_rd_11_15, ir_4_rt_16_20;
  wire [5:0] ir_1_op_26_31, ir_2_op_26_31, ir_3_op_26_31, ir_4_op_26_31;

  Comparator #(.width(32)) comparator_1 (.a(I_ID), .b(32'hc), .eq(R_sys));  // open: gt, lt
  Comparator #(.width(32)) comparator_2 (.a(I_ID), .b({32{1'b0}}), .eq(R_nop));  // open: gt, lt
  Read_Reg read_reg_1 (
    .Op6(ir_2_op_26_31[5]), .Op5(ir_2_op_26_31[4]), .Op4(ir_2_op_26_31[3]), .Op3(ir_2_op_26_31[2]),
    .Op2(ir_2_op_26_31[1]), .Op1(ir_2_op_26_31[0]), .Rt_W(read_reg_1_rt_w), .Rd_W(read_reg_1_rd_w));  // open: Rs, Rt
  Comparator #(.width(32)) comparator_3 (.a(I_EX), .b({32{1'b0}}), .eq(EX_nop));  // open: gt, lt
  Comparator #(.width(32)) comparator_4 (.a(I_EX), .b(32'hc), .eq(EX_sys));  // open: gt, lt
  Read_Reg read_reg_2 (
    .Op6(ir_3_op_26_31[5]), .Op5(ir_3_op_26_31[4]), .Op4(ir_3_op_26_31[3]), .Op3(ir_3_op_26_31[2]),
    .Op2(ir_3_op_26_31[1]), .Op1(ir_3_op_26_31[0]), .Rt_W(read_reg_2_rt_w), .Rd_W(read_reg_2_rd_w));  // open: Rs, Rt
  Comparator #(.width(32)) comparator_5 (.a(I_Mem), .b({32{1'b0}}), .eq(Mem_nop));  // open: gt, lt
  Comparator #(.width(32)) comparator_6 (.a(I_Mem), .b(32'hc), .eq(Mem_sys));  // open: gt, lt
  Read_Reg read_reg_3 (
    .Op6(ir_4_op_26_31[5]), .Op5(ir_4_op_26_31[4]), .Op4(ir_4_op_26_31[3]), .Op3(ir_4_op_26_31[2]),
    .Op2(ir_4_op_26_31[1]), .Op1(ir_4_op_26_31[0]), .Rt_W(read_reg_3_rt_w), .Rd_W(read_reg_3_rd_w));  // open: Rs, Rt
  Comparator #(.width(32)) comparator_7 (.a(I_WB), .b({32{1'b0}}), .eq(WB_nop));  // open: gt, lt
  Comparator #(.width(32)) comparator_8 (.a(I_WB), .b(32'hc), .eq(WB_sys));  // open: gt, lt
  IR ir_1 (
    .in_1(I_ID), .Rs_21_25(ir_1_rs_21_25), .Rt_16_20(ir_1_rt_16_20), .Op_26_31(ir_1_op_26_31));  // open: Rd_11_15, IM_0_15, l26_0_25, funct_0_5, shmat_6_10
  IR ir_2 (
    .in_1(I_EX), .Rt_16_20(ir_2_rt_16_20), .Rd_11_15(ir_2_rd_11_15), .Op_26_31(ir_2_op_26_31));  // open: Rs_21_25, IM_0_15, l26_0_25, funct_0_5, shmat_6_10
  IR ir_3 (
    .in_1(I_Mem), .Rt_16_20(ir_3_rt_16_20), .Rd_11_15(ir_3_rd_11_15), .Op_26_31(ir_3_op_26_31));  // open: Rs_21_25, IM_0_15, l26_0_25, funct_0_5, shmat_6_10
  Read_Reg read_reg_4 (
    .Op6(ir_1_op_26_31[5]), .Op5(ir_1_op_26_31[4]), .Op4(ir_1_op_26_31[3]), .Op3(ir_1_op_26_31[2]),
    .Op2(ir_1_op_26_31[1]), .Op1(ir_1_op_26_31[0]), .Rs(Rs_R), .Rt(Rt_R));  // open: Rt_W, Rd_W
  IR ir_4 (
    .in_1(I_WB), .Rt_16_20(ir_4_rt_16_20), .Rd_11_15(ir_4_rd_11_15), .Op_26_31(ir_4_op_26_31));  // open: Rs_21_25, IM_0_15, l26_0_25, funct_0_5, shmat_6_10
  or or_1 (or_1_out, or_4_out, or_2_out);
  RelativeCompare relativecompare_1 (
    .in_1(ir_1_rs_21_25), .in_4(ir_1_rt_16_20), .in_6(ir_2_rt_16_20), .in_8(ir_2_rd_11_15), .out_10(out_5),
    .R_Rs(Rs_R), .R_Rt(Rt_R), .W_Rt(read_reg_1_rt_w), .W_Rd(read_reg_1_rd_w), .in_2(or_1_out));
  RelativeCompare relativecompare_2 (
    .in_1(ir_1_rs_21_25), .in_4(ir_1_rt_16_20), .in_6(ir_3_rt_16_20), .in_8(ir_3_rd_11_15), .out_10(out_6),
    .R_Rs(Rs_R), .R_Rt(Rt_R), .W_Rt(read_reg_2_rt_w), .W_Rd(read_reg_2_rd_w), .in_2(or_3_out));
  RelativeCompare relativecompare_3 (
    .in_1(ir_1_rs_21_25), .in_4(ir_1_rt_16_20), .in_6(ir_4_rt_16_20), .in_8(ir_4_rd_11_15), .out_10(out_7),
    .R_Rs(Rs_R), .R_Rt(Rt_R), .W_Rt(read_reg_3_rt_w), .W_Rd(read_reg_3_rd_w), .in_2(or_8_out));
  or or_2 (or_2_out, EX_sys, R_sys);
  or or_3 (or_3_out, or_5_out, or_6_out);
  or or_4 (or_4_out, R_nop, EX_nop);
  or or_5 (or_5_out, R_nop, Mem_nop);
  or or_6 (or_6_out, Mem_sys, R_sys);
  or or_7 (or_7_out, R_nop, WB_nop);
  or or_8 (or_8_out, or_7_out, or_9_out);
  or or_9 (or_9_out, WB_sys, R_sys);
endmodule

module RelativeCompare (
  input  [4:0] in_1,
  input  in_2,
  input  R_Rs,
  input  [4:0] in_4,
  input  R_Rt,
  input  [4:0] in_6,
  input  W_Rt,
  input  [4:0] in_8,
  input  W_Rd,
  output out_10
);

  wire and_1_out, and_2_out, and_3_out, and_4_out, and_5_out, and_6_out, and_7_out, and_8_out,
       comparator_1_eq, comparator_2_eq, comparator_3_eq, comparator_4_eq, comparator_5_eq, comparator_6_eq,
       not_1_out, or_1_out;

  and and_1 (and_1_out, R_Rs, W_Rt);
  and and_2 (and_2_out, W_Rd, R_Rs);
  and and_3 (and_3_out, R_Rt, W_Rt);
  and and_4 (and_4_out, R_Rt, W_Rd);
  Comparator #(.width(5)) comparator_1 (.a(in_1), .b(in_6), .eq(comparator_1_eq));  // open: gt, lt
  Comparator #(.width(5)) comparator_2 (.a(in_1), .b(in_8), .eq(comparator_2_eq));  // open: gt, lt
  Comparator #(.width(5)) comparator_3 (.a(in_4), .b(in_6), .eq(comparator_3_eq));  // open: gt, lt
  Comparator #(.width(5)) comparator_4 (.a(in_4), .b(in_8), .eq(comparator_4_eq));  // open: gt, lt
  and and_5 (and_5_out, comparator_2_eq, and_2_out);
  and and_6 (and_6_out, comparator_3_eq, and_3_out);
  and and_7 (and_7_out, comparator_4_eq, and_4_out);
  and and_8 (and_8_out, comparator_1_eq, and_1_out);
  Comparator #(.width(5)) comparator_5 (.a(in_6), .b(5'b00010), .eq(comparator_5_eq));  // open: gt, lt
  Comparator #(.width(5)) comparator_6 (.a(in_8), .b(5'b00010), .eq(comparator_6_eq));  // open: gt, lt
  not not_1 (not_1_out, in_2);
  and and_9 (out_10, not_1_out, or_1_out);
  or or_1 (or_1_out, and_8_out, and_5_out, and_6_out, and_7_out);
  // OR_Gate or_2 has open pins: in0=comparator_5_eq, in1=comparator_6_eq, out=open
endmodule

module Read_Reg (
  input  Op6,
  input  Op5,
  input  Op4,
  input  Op3,
  input  Op2,
  input  Op1,
  output Rs,
  output Rt,
  output Rt_W,
  output Rd_W
);

  wire and_1_out, and_2_out, and_3_out, and_4_out, and_5_out, and_6_out, and_7_out, and_8_out, and_9_out,
       and_10_out, and_11_out, not_1_out, not_2_out, not_3_out, not_4_out, not_5_out, not_6_out, not_7_out,
       not_8_out, not_9_out, not_10_out, not_11_out, not_12_out, not_13_out, not_14_out, not_15_out,
       not_16_out, not_17_out, not_18_out, not_19_out, not_20_out, not_21_out, not_22_out, not_23_out,
       not_24_out, not_25_out, not_26_out, not_27_out, not_28_out, not_29_out, not_30_out, not_31_out,
       not_32_out, not_33_out, not_34_out, not_35_out, not_36_out, not_37_out, not_38_out, not_39_out,
       not_40_out, not_41_out, not_42_out;

  not not_1 (not_1_out, Op6);
  not not_2 (not_2_out, Op5);
  not not_3 (not_3_out, Op2);
  not not_4 (not_4_out, Op5);
  not not_5 (not_5_out, Op4);
  not not_6 (not_6_out, Op3);
  not not_7 (not_7_out, Op2);
  not not_8 (not_8_out, Op6);
  not not_9 (not_9_out, Op5);
  not not_10 (not_10_out, Op3);
  not not_11 (not_11_out, Op1);
  not not_12 (not_12_out, Op5);
  not not_13 (not_13_out, Op3);
  not not_14 (not_14_out, Op6);
  not not_15 (not_15_out, Op5);
  not not_16 (not_16_out, Op4);
  not not_17 (not_17_out, Op2);
  not not_18 (not_18_out, Op1);
  not not_19 (not_19_out, Op6);
  not not_20 (not_20_out, Op5);
  not not_21 (not_21_out, Op4);
  not not_22 (not_22_out, Op2);
  not not_23 (not_23_out, Op5);
  not not_24 (not_24_out, Op3);
  not not_25 (not_25_out, Op6);
  not not_26 (not_26_out, Op5);
  not not_27 (not_27_out, Op3);
  not not_28 (not_28_out, Op1);
  not not_29 (not_29_out, Op6);
  not not_30 (not_30_out, Op5);
  not not_31 (not_31_out, Op2);
  not not_32 (not_32_out, Op6);
  not not_33 (not_33_out, Op5);
  not not_34 (not_34_out, Op5);
  not not_35 (not_35_out, Op4);
  not not_36 (not_36_out, Op3);
  not not_37 (not_37_out, Op6);
  not not_38 (not_38_out, Op5);
  not not_39 (not_39_out, Op4);
  not not_40 (not_40_out, Op3);
  not not_41 (not_41_out, Op2);
  not not_42 (not_42_out, Op1);
  and and_1 (and_1_out, not_1_out, not_2_out, not_3_out);
  and and_2 (and_2_out, not_4_out, not_5_out, not_6_out, not_7_out, Op1);
  and and_3 (and_3_out, not_8_out, not_9_out, Op4, not_10_out, not_11_out);
  and and_4 (and_4_out, Op6, not_12_out, not_13_out, Op2, Op1);
  and and_5 (and_5_out, not_14_out, not_15_out, not_16_out, not_17_out, not_18_out);
  and and_6 (and_6_out, not_19_out, not_20_out, not_21_out, Op3, not_22_out);
  and and_7 (and_7_out, Op6, not_23_out, Op4, not_24_out, Op2, Op1);
  and and_8 (and_8_out, not_25_out, not_26_out, Op4, not_27_out, not_28_out);
  and and_9 (and_9_out, not_29_out, not_30_out, Op4, not_31_out);
  and and_10 (and_10_out, not_32_out, not_33_out, Op4, Op3, Op1);
  and and_11 (and_11_out, Op6, not_34_out, not_35_out, not_36_out, Op1);
  and and_12 (Rd_W, not_37_out, not_38_out, not_39_out, not_40_out, not_41_out, not_42_out);
  or or_1 (Rs, and_1_out, and_2_out, and_3_out, and_4_out);
  or or_2 (Rt, and_5_out, and_6_out, and_7_out);
  or or_3 (Rt_W, and_8_out, and_9_out, and_10_out, and_11_out);
endmodule
