// Logisim project CS1401_U201414573_朱珺_alu.circ as structural Verilog: 21 circuits, main circuit ALU
module ALU (
  input  [31:0] X,
  input  [31:0] Y,
  input  [3:0] AluOP,
  output Signed_Overflow,
  output UnSigned_Overflow,
  output Equal,
  output [31:0] Result,
  output [31:0] Result_2
);

  wire OF6, OF7, UOF6, UOF7;
  wire [0:0] Result_12, Result_13;
  wire [31:0] Result2_4, Result2_5, Result_1, Result_2_t, Result_3, Result_4, Result_5, Result_6, Result_7,
       Result_8, Result_9, Result_10, Result_11, x_func1, x_func2, x_func3, x_func4, x_func5, x_func6,
       x_func7, x_func8, x_func9, x_func10, x_func11, x_func12, x_func13, y_func1, y_func2, y_func3, y_func4,
       y_func5, y_func6, y_func7, y_func8, y_func9, y_func10, y_func11, y_func12, y_func13;

  // Probe on X
  // Probe on X
  // Probe on Y
  // Probe on Y
  Demultiplexer #(.select(4), .width(32)) demultiplexer_1 (
    .out0(x_func1), .out1(x_func2), .out2(x_func3), .out3(x_func4), .out4(x_func5), .out5(x_func6),
    .out6(x_func7), .out7(x_func8), .out8(x_func9), .out9(x_func10), .out10(x_func11), .out11(x_func12),
    .out12(x_func13), .in(X), .sel(AluOP), .en(1'b1));  // open: out13, out14, out15
  Demultiplexer #(.select(4), .width(32), .disabled(0)) demultiplexer_2 (
    .out0(y_func1), .out1(y_func2), .out2(y_func3), .out3(y_func4), .out4(y_func5), .out5(y_func6),
    .out6(y_func7), .out7(y_func8), .out8(y_func9), .out9(y_func10), .out10(y_func11), .out11(y_func12),
    .out12(y_func13), .in(Y), .sel(AluOP), .en(1'b1));  // open: out13, out14, out15
  Comparator #(.width(32), .mode("unsigned")) comparator_1 (.a(X), .b(Y), .eq(Equal));  // open: gt, lt
  // Probe on AluOP
  // Probe on Result
  // Probe on Result
  \func1_逻辑左  \func1_逻辑左_1  (.in_1(x_func1), .in_2(y_func1), .out_3(Result_1));
  \func3_逻辑右  \func3_逻辑右_1  (.in_1(x_func3), .in_2(y_func3), .out_3(Result_3));
  \func5_无符号64位除法  \func5_无符号64位除法_1  (.in_1(x_func5), .in_2(y_func5), .out_3(Result_5), .out_4(Result2_5));
  \func7_减法器  \func7_减法器_1  (.in_1(x_func7), .in_2(y_func7), .out_3(Result_7), .OF(OF7), .UOF(UOF7));
  \func9_按位或  \func9_按位或_1  (.in_1(x_func9), .in_2(y_func9), .out(Result_9));
  \func11_按位或非  \func11_按位或非_1  (.in_1(x_func11), .in_2(y_func11), .out(Result_11));
  \func13_无符号比较  \func13_无符号比较_1  (.in_1(x_func13), .in_2(y_func13), .out(Result_13[0]));
  // Probe on Result_2
  \func2_算术右  \func2_算术右_1  (.in_1(x_func2), .in_2(y_func2), .out_3(Result_2_t));
  \func6_加法器  \func6_加法器_1  (.in_1(x_func6), .in_2(y_func6), .out_3(Result_6), .OF(OF6), .UOF(UOF6));
  \func8_按位与  \func8_按位与_1  (.in_1(x_func8), .in_2(y_func8), .out(Result_8));
  \func10_按位异或  \func10_按位异或_1  (.in_1(x_func10), .in_2(y_func10), .out(Result_10));
  \func12_有符号比较  \func12_有符号比较_1  (.in_1(x_func12), .in_2(y_func12), .out(Result_12[0]));
  \func4_有符号64位乘法  \func4_有符号64位乘法_1  (.in_1(x_func4), .in_2(y_func4), .out_3(Result_4), .out_4(Result2_4));
  Multiplexer #(.select(4), .width(32)) multiplexer_1 (
    .in0(Result_1), .in1(Result_2_t), .in2(Result_3), .in3(Result_4), .in4(Result_5), .in5(Result_6),
    .in6(Result_7), .in7(Result_8), .in8(Result_9), .in9(Result_10), .in10(Result_11),
    .in11({{31{1'b0}}, Result_12[0]}), .in12({{31{1'b0}}, Result_13[0]}), .in13({32{1'b0}}),
    .in14({32{1'b0}}), .in15({32{1'b0}}), .out(Result), .sel(AluOP), .en(1'b1));
  Multiplexer #(.select(4), .width(32)) multiplexer_2 (
    .in0({32{1'b0}}), .in1({32{1'b0}}), .in2({32{1'b0}}), .in3(Result2_4), .in4(Result2_5), .in5({32{1'b0}}),
    .in6({32{1'b0}}), .in7({32{1'b0}}), .in8({32{1'b0}}), .in9({32{1'b0}}), .in10({32{1'b0}}),
    .in11({32{1'b0}}), .in12({32{1'b0}}), .in13({32{1'b0}}), .in14({32{1'b0}}), .in15({32{1'b0}}),
    .out(Result_2), .sel(AluOP), .en(1'b1));
  Multiplexer #(.select(4)) multiplexer_3 (
    .in0(1'b0), .in1(1'b0), .in2(1'b0), .in3(1'b0), .in4(1'b0), .in5(UOF6), .in6(UOF7), .in7(1'b0),
    .in8(1'b0), .in9(1'b0), .in10(1'b0), .in11(1'b0), .in12(1'b0), .in13(1'b0), .in14(1'b0), .in15(1'b0),
    .out(UnSigned_Overflow), .sel(AluOP), .en(1'b1));
  Multiplexer #(.select(4)) multiplexer_4 (
    .in0(1'b0), .in1(1'b0), .in2(1'b0), .in3(1'b0), .in4(1'b0), .in5(OF6), .in6(OF7), .in7(1'b0), .in8(1'b0),
    .in9(1'b0), .in10(1'b0), .in11(1'b0), .in12(1'b0), .in13(1'b0), .in14(1'b0), .in15(1'b0),
    .out(Signed_Overflow), .sel(AluOP), .en(1'b1));

  // Other names for the same wires on the sheet: OF = Signed_Overflow; Result2[31:0] = Result_2; S[3:0] = AluOP;
  //   UOF = UnSigned_Overflow

  // Notes on the sheet:
  //   不要改变此引脚区域内容，也不要改变ALU封装形式
  //   输入引脚
  //   请在下方利用上方输入输出引脚的隧道信号构建ALU电路，ctrl+d复制选择部件
  //   华中科技大学计算机学院 计算机组成原理，鸣谢加州大学伯克利CS61C课程
  //   输出引脚
  //   探测区域
endmodule

module \演示电路  (
  input  [31:0] X,
  input  [31:0] Y,
  input  [3:0] ALUOP,
  output Signed_Overflow,
  output Unsigned_overflow,
  output [31:0] Result,
  output [31:0] Result_2,
  output Equal
);

  // Probe on X
  // Probe on X
  ALU alu_1 (
    .AluOP(ALUOP), .X(X), .Equal(Equal), .Result(Result), .Signed_Overflow(Signed_Overflow), .Y(Y),
    .Result_2(Result_2), .UnSigned_Overflow(Unsigned_overflow));
  // Probe on ALUOP
  // Probe on Y
  // Probe on Y
  // Probe on Result
  // Probe on Result
  // Probe on Result_2

  // Notes on the sheet:
  //   ALu电路无需调整位置即可连接在该电路中，并且不能出现蓝色线缆和三态输出
endmodule

module \等差数列  (
  input  [31:0] \数列初始值 ,
  input  [31:0] \等差值 ,
  input  \时钟 ,
  output [31:0] Result
);

  // Probe on \数列初始值 
  // Probe on \数列初始值 
  // Probe on \等差值 
  // Probe on \等差值 
  // Probe on Result
  // Probe on Result

  // Other names for the same wires on the sheet: 数列初值[31:0] = \数列初始值 ; 累加和[31:0] = Result

  // Notes on the sheet:
  //   不要改变此引脚区域内容，也不要改变ALU封装形式
  //   请在下方利用上方输入输出引脚的隧道信号构建等差数列求和电路，ctrl+d复制选择部件
  //   华中科技大学计算机学院 计算机组成原理，鸣谢加州大学伯克利CS61C课程
  //   输出引脚
  //   探测区域
endmodule

module PG (
  input  [3:0] in_1,
  input  [3:0] in_2,
  output G4,
  output P4,
  output G3,
  output P3,
  output G2,
  output P2,
  output G1,
  output P1
);

  and and_1 (G4, in_1[3], in_2[3]);
  xor xor_1 (P4, in_1[3], in_2[3]);
  and and_2 (G3, in_1[2], in_2[2]);
  xor xor_2 (P3, in_1[2], in_2[2]);
  and and_3 (G2, in_1[1], in_2[1]);
  xor xor_3 (P2, in_1[1], in_2[1]);
  and and_4 (G1, in_1[0], in_2[0]);
  xor xor_4 (P1, in_1[0], in_2[0]);
endmodule

module _74182 (
  input  Cn,
  input  G4,
  input  P4,
  input  G3,
  input  P3,
  input  G2,
  input  P2,
  input  G1,
  input  P1,
  output C4,
  output G_star,
  output C3,
  output C2,
  output C1,
  output P_star
);

  wire and_1_out, and_2_out, and_3_out, and_4_out, and_5_out, and_6_out, and_7_out, and_8_out, and_9_out,
       and_10_out;

  or or_1 (C4, and_1_out, G4, and_3_out, and_2_out, and_4_out);
  and and_1 (and_1_out, P4, P3, P2, P1, Cn);
  or or_2 (G_star, G4, and_3_out, and_2_out, and_4_out);
  and and_2 (and_2_out, P4, P3, G2);
  and and_3 (and_3_out, P4, G3);
  and and_4 (and_4_out, P4, P3, P2, G1);
  or or_3 (C3, G3, and_5_out, and_7_out, and_6_out);
  and and_5 (and_5_out, P3, G2);
  and and_6 (and_6_out, P3, P2, P1, Cn);
  and and_7 (and_7_out, P3, P2, G1);
  or or_4 (C2, G2, and_8_out, and_9_out);
  and and_8 (and_8_out, P2, G1);
  and and_9 (and_9_out, P2, P1, Cn);
  or or_5 (C1, G1, and_10_out);
  and and_10 (and_10_out, P1, Cn);
  and and_11 (P_star, P1, P2, P3, P4);
endmodule

module _74181 (
  input  C,
  input  [3:0] A,
  input  [3:0] B,
  output G,
  output P,
  output [3:0] F,
  output C3
);

  wire n74182_1_c1, n74182_1_c2, pg_1_g1, pg_1_g2, pg_1_g3, pg_1_g4, pg_1_p1, pg_1_p2, pg_1_p3, pg_1_p4;

  PG pg_1 (
    .G4(pg_1_g4), .P4(pg_1_p4), .G3(pg_1_g3), .P3(pg_1_p3), .G2(pg_1_g2), .P2(pg_1_p2), .G1(pg_1_g1),
    .P1(pg_1_p1), .in_1(A), .in_2(B));
  xor xor_1 (F[0], C, pg_1_p1);
  _74182 u_74182_1 (
    .Cn(C), .G_star(G), .C3(C3), .C2(n74182_1_c2), .C1(n74182_1_c1), .P_star(P), .G4(pg_1_g4), .P4(pg_1_p4),
    .G3(pg_1_g3), .P3(pg_1_p3), .G2(pg_1_g2), .P2(pg_1_p2), .G1(pg_1_g1), .P1(pg_1_p1));  // open: C4
  xor xor_2 (F[1], n74182_1_c1, pg_1_p2);
  xor xor_3 (F[2], n74182_1_c2, pg_1_p3);
  xor xor_4 (F[3], C3, pg_1_p4);
endmodule

module \_16位全并行  (
  input  C0,
  input  [15:0] B,
  input  [15:0] A,
  output G_star,
  output P_star,
  output C4,
  output [15:0] F,
  output C3
);

  wire n74181_1_g, n74181_1_p, n74181_2_g, n74181_2_p, n74181_3_g, n74181_3_p, n74181_4_g, n74181_4_p,
       n74182_1_c1, n74182_1_c2, n74182_1_c3;

  _74181 u_74181_1 (.C3(C3), .C(n74182_1_c3), .G(n74181_1_g), .P(n74181_1_p), .F(F[15:12]), .A(A[15:12]), .B(B[15:12]));
  _74181 u_74181_2 (
    .C(n74182_1_c2), .G(n74181_2_g), .P(n74181_2_p), .F(F[11:8]), .A(A[11:8]), .B(B[11:8]));  // open: C3
  _74182 u_74182_1 (
    .C4(C4), .Cn(C0), .G_star(G_star), .C3(n74182_1_c3), .C2(n74182_1_c2), .C1(n74182_1_c1), .P_star(P_star),
    .G4(n74181_1_g), .P4(n74181_1_p), .G3(n74181_2_g), .P3(n74181_2_p), .G2(n74181_3_g), .P2(n74181_3_p),
    .G1(n74181_4_g), .P1(n74181_4_p));
  _74181 u_74181_3 (.C(n74182_1_c1), .G(n74181_3_g), .P(n74181_3_p), .F(F[7:4]), .A(A[7:4]), .B(B[7:4]));  // open: C3
  _74181 u_74181_4 (.C(C0), .G(n74181_4_g), .P(n74181_4_p), .F(F[3:0]), .A(A[3:0]), .B(B[3:0]));  // open: C3
endmodule

module \_32位全并行  (
  input  [31:0] A,
  input  [31:0] B,
  output UOF,
  output [31:0] F,
  output OF
);

  wire \n16位全并行_1_c3 , \n16位全并行_1_g_star , \n16位全并行_1_p_star , \n16位全并行_2_g_star , \n16位全并行_2_p_star ,
       n74182_1_c1;

  xor xor_1 (OF, UOF, \n16位全并行_1_c3 );
  \_16位全并行  \u_16位全并行_1  (
    .C4(UOF), .C3(\n16位全并行_1_c3 ), .A(A[31:16]), .F(F[31:16]), .C0(n74182_1_c1), .B(B[31:16]),
    .G_star(\n16位全并行_1_g_star ), .P_star(\n16位全并行_1_p_star ));
  _74182 u_74182_1 (
    .Cn(1'b0), .C1(n74182_1_c1), .G4(1'b0), .P4(1'b0), .G3(1'b0), .P3(1'b0), .G2(\n16位全并行_1_g_star ),
    .P2(\n16位全并行_1_p_star ), .G1(\n16位全并行_2_g_star ), .P1(\n16位全并行_2_p_star ));  // open: C4, G_star, C3, C2, P_star
  \_16位全并行  \u_16位全并行_2  (
    .A(A[15:0]), .F(F[15:0]), .C0(1'b0), .B(B[15:0]), .G_star(\n16位全并行_2_g_star ), .P_star(\n16位全并行_2_p_star ));  // open: C4, C3
endmodule

module \func1_逻辑左  (
  input  [31:0] in_1,
  input  [31:0] in_2,
  output [31:0] out_3
);

  Shifter #(.width(32)) shifter_1 (.in(in_1), .\dist (in_2[4:0]), .out(out_3));
endmodule

module \func2_算术右  (
  input  [31:0] in_1,
  input  [31:0] in_2,
  output [31:0] out_3
);

  Shifter #(.width(32), .shift("ar")) shifter_1 (.in(in_1), .\dist (in_2[4:0]), .out(out_3));
endmodule

module \func3_逻辑右  (
  input  [31:0] in_1,
  input  [31:0] in_2,
  output [31:0] out_3
);

  Shifter #(.width(32), .shift("lr")) shifter_1 (.in(in_1), .\dist (in_2[4:0]), .out(out_3));
endmodule

module \func4_有符号64位乘法  (
  input  [31:0] in_1,
  input  [31:0] in_2,
  output [31:0] out_3,
  output [31:0] out_4
);

  // Probe on in_1
  // Probe on in_2
  // Probe on out_3
  Multiplier #(.width(32)) multiplier_1 (.a(in_1), .b(in_2), .out(out_3), .cout(out_4));  // open: cin
  // Probe on out_4
endmodule

module \func5_无符号64位除法  (
  input  [31:0] in_1,
  input  [31:0] in_2,
  output [31:0] out_3,
  output [31:0] out_4
);

  Divider #(.width(32)) divider_1 (.a(in_1), .b(in_2), .out(out_3), .rem(out_4));  // open: upper
endmodule

module \func6_加法器  (
  input  [31:0] in_1,
  input  [31:0] in_2,
  output [31:0] out_3,
  output OF,
  output UOF
);

  wire \n32位全并行_1_uof ;

  \_32位全并行  \u_32位全并行_1  (.UOF(\n32位全并行_1_uof ), .OF(OF), .A(in_1), .B(in_2), .F(out_3));
  xor xor_1 (UOF, \n32位全并行_1_uof , 1'b0);
endmodule

module \func7_减法器  (
  input  [31:0] in_1,
  input  [31:0] in_2,
  output [31:0] out_3,
  output OF,
  output UOF
);

  wire \n32位全并行_1_uof ;
  wire [31:0] negator_1_out;

  Negator #(.width(32)) negator_1 (.in(in_2), .out(negator_1_out));
  \_32位全并行  \u_32位全并行_1  (.UOF(\n32位全并行_1_uof ), .OF(OF), .A(in_1), .B(negator_1_out), .F(out_3));
  xor xor_1 (UOF, \n32位全并行_1_uof , 1'b1);
endmodule

module \func8_按位与  (
  input  [31:0] in_1,
  input  [31:0] in_2,
  output [31:0] out
);

  assign out = in_1 & in_2;  // AND_Gate and_1, 32 bits wide
endmodule

module \func9_按位或  (
  input  [31:0] in_1,
  input  [31:0] in_2,
  output [31:0] out
);

  assign out = in_1 | in_2;  // OR_Gate or_1, 32 bits wide
endmodule

module \func10_按位异或  (
  input  [31:0] in_1,
  input  [31:0] in_2,
  output [31:0] out
);

  assign out = in_1 ^ in_2;  // XOR_Gate xor_1, 32 bits wide
endmodule

module \func11_按位或非  (
  input  [31:0] in_1,
  input  [31:0] in_2,
  output [31:0] out
);

  assign out = ~(in_1 | in_2);  // NOR_Gate nor_1, 32 bits wide
endmodule

module \func12_有符号比较  (
  input  [31:0] in_1,
  input  [31:0] in_2,
  output out
);

  Comparator #(.width(32)) comparator_1 (.a(in_1), .b(in_2), .lt(out));  // open: gt, eq
endmodule

module \func13_无符号比较  (
  input  [31:0] in_1,
  input  [31:0] in_2,
  output out
);

  Comparator #(.width(32), .mode("unsigned")) comparator_1 (.a(in_1), .b(in_2), .lt(out));  // open: gt, eq
endmodule
