// Logisim project regfile2.circ as structural Verilog: 4 circuits, main circuit main
module main (
  input  [4:0] Reg1_num,
  input  [4:0] Reg2,
  input  [4:0] Write_Reg_num,
  input  [31:0] Din,
  input  Write_Enable,
  input  Clock,
  output [31:0] Reg1,
  output [31:0] s0_Value,
  output [31:0] s1_Value,
  output [31:0] s2_Value,
  output [31:0] ra_Value,
  output [31:0] Reg2_2
);

  wire r1, r2, r3, r4, r5, r6, r7, r8, r9, r10, r11, r12, r13, r14, r15, r16, r17, r18, r19, r20, r21, r22,
       r23, r24, r25, r26, r27, r28, r29, r30, r31;
  wire [31:0] out0, out1, out3, out5, out6, out7, out8, out9, out10, out11, out12, out13, out14, out15,
       out16, out17, out19, out20, out21, out22, out23, out24, out25, out26, out27, out28, out29, out30;

  Demultiplexer #(.select(5), .disabled(0), .enable("false")) demultiplexer_1 (
    .out1(r1), .out2(r2), .out3(r3), .out4(r4), .out5(r5), .out6(r6), .out7(r7), .out8(r8), .out9(r9),
    .out10(r10), .out11(r11), .out12(r12), .out13(r13), .out14(r14), .out15(r15), .out16(r16), .out17(r17),
    .out18(r18), .out19(r19), .out20(r20), .out21(r21), .out22(r22), .out23(r23), .out24(r24), .out25(r25),
    .out26(r26), .out27(r27), .out28(r28), .out29(r29), .out30(r30), .out31(r31), .in(Write_Enable),
    .sel(Write_Reg_num));  // open: out0
  Multiplexer #(.select(5), .width(32)) multiplexer_1 (
    .in0(out0), .in1(out1), .in2(s0_Value), .in3(out3), .in4(s1_Value), .in5(out5), .in6(out6), .in7(out7),
    .in8(out8), .in9(out9), .in10(out10), .in11(out11), .in12(out12), .in13(out13), .in14(out14),
    .in15(out15), .in16(out16), .in17(out17), .in18(s2_Value), .in19(out19), .in20(out20), .in21(out21),
    .in22(out22), .in23(out23), .in24(out24), .in25(out25), .in26(out26), .in27(out27), .in28(out28),
    .in29(out29), .in30(out30), .in31(ra_Value), .out(Reg1), .sel(Reg1_num), .en(1'b1));
  Multiplexer #(.select(5), .width(32)) multiplexer_2 (
    .in0(out0), .in1(out1), .in2(s0_Value), .in3(out3), .in4(s1_Value), .in5(out5), .in6(out6), .in7(out7),
    .in8(out8), .in9(out9), .in10(out10), .in11(out11), .in12(out12), .in13(out13), .in14(out14),
    .in15(out15), .in16(out16), .in17(out17), .in18(s2_Value), .in19(out19), .in20(out20), .in21(out21),
    .in22(out22), .in23(out23), .in24(out24), .in25(out25), .in26(out26), .in27(out27), .in28(out28),
    .in29(out29), .in30(out30), .in31(ra_Value), .out(Reg2_2), .sel(Reg2), .en(1'b1));
  Register #(.width(32)) register_1 (.D(Din), .en(r1), .Q(out1), .clk(Clock), .clr(1'b0));
  Register #(.width(32)) register_2 (.D(Din), .en(r2), .Q(s0_Value), .clk(Clock), .clr(1'b0));
  Register #(.width(32)) register_3 (.D(Din), .en(r3), .Q(out3), .clk(Clock), .clr(1'b0));
  Register #(.width(32)) register_4 (.D(Din), .en(r4), .Q(s1_Value), .clk(Clock), .clr(1'b0));
  Register #(.width(32)) register_5 (.D(Din), .en(r5), .Q(out5), .clk(Clock), .clr(1'b0));
  Register #(.width(32)) register_6 (.D(Din), .en(r6), .Q(out6), .clk(Clock), .clr(1'b0));
  Register #(.width(32)) register_7 (.D(Din), .en(r7), .Q(out7), .clk(Clock), .clr(1'b0));
  Register #(.width(32)) register_8 (.D(Din), .en(r8), .Q(out8), .clk(Clock), .clr(1'b0));
  Register #(.width(32)) register_9 (.D(Din), .en(r9), .Q(out9), .clk(Clock), .clr(1'b0));
  Register #(.width(32)) register_10 (.D(Din), .en(r10), .Q(out10), .clk(Clock), .clr(1'b0));
  Register #(.width(32)) register_11 (.D(Din), .en(r11), .Q(out11), .clk(Clock), .clr(1'b0));
  Register #(.width(32)) register_12 (.D(Din), .en(r12), .Q(out12), .clk(Clock), .clr(1'b0));
  Register #(.width(32)) register_13 (.D(Din), .en(r13), .Q(out13), .clk(Clock), .clr(1'b0));
  Register #(.width(32)) register_14 (.D(Din), .en(r14), .Q(out14), .clk(Clock), .clr(1'b0));
  Register #(.width(32)) register_15 (.D(Din), .en(r15), .Q(out15), .clk(Clock), .clr(1'b0));
  Register #(.width(32)) register_16 (.D(Din), .en(r16), .Q(out16), .clk(Clock), .clr(1'b0));
  Register #(.width(32)) register_17 (.D(Din), .en(r17), .Q(out17), .clk(Clock), .clr(1'b0));
  Register #(.width(32)) register_18 (.D(Din), .en(r18), .Q(s2_Value), .clk(Clock), .clr(1'b0));
  Register #(.width(32)) register_19 (.D(Din), .en(r19), .Q(out19), .clk(Clock), .clr(1'b0));
  Register #(.width(32)) register_20 (.D(Din), .en(r20), .Q(out20), .clk(Clock), .clr(1'b0));
  Register #(.width(32)) register_21 (.D(Din), .en(r21), .Q(out21), .clk(Clock), .clr(1'b0));
  Register #(.width(32)) register_22 (.D(Din), .en(r22), .Q(out22), .clk(Clock), .clr(1'b0));
  Register #(.width(32)) register_23 (.D(Din), .en(r23), .Q(out23), .clk(Clock), .clr(1'b0));
  Register #(.width(32)) register_24 (.D(Din), .en(r24), .Q(out24), .clk(Clock), .clr(1'b0));
  Register #(.width(32)) register_25 (.D(Din), .en(r25), .Q(out25), .clk(Clock), .clr(1'b0));
  Register #(.width(32)) register_26 (.D(Din), .en(r26), .Q(out26), .clk(Clock), .clr(1'b0));
  Register #(.width(32)) register_27 (.D(Din), .en(r27), .Q(out27), .clk(Clock), .clr(1'b0));
  Register #(.width(32)) register_28 (.D(Din), .en(r28), .Q(out28), .clk(Clock), .clr(1'b0));
  Register #(.width(32)) register_29 (.D(Din), .en(r29), .Q(out29), .clk(Clock), .clr(1'b0));
  Register #(.width(32)) register_30 (.D(Din), .en(r30), .Q(out30), .clk(Clock), .clr(1'b0));
  Register #(.width(32)) register_31 (.D(Din), .en(r31), .Q(ra_Value), .clk(Clock), .clr(1'b0));
  Register #(.width(32)) register_32 (.D({32{1'b0}}), .en(Write_Enable), .Q(out0), .clk(Clock), .clr(1'b0));

  // Other names for the same wires on the sheet: clk = Clock; out2[31:0] = s0_Value; s0[31:0] = s0_Value;
  //   out4[31:0] = s1_Value; s1[31:0] = s1_Value; out18[31:0] = s2_Value; s2[31:0] = s2_Value; out31[31:0] = ra_Value;
  //   ra[31:0] = ra_Value; reg2_num[4:0] = Reg2; reg2_t[31:0] = Reg2_2; WE = Write_Enable; write_data[31:0] = Din

  // Notes on the sheet:
  //   输入引脚
  //   输出引脚
  //   Debug引脚，便于观测寄存器值
  //   请勿修改引脚以及封装，直接使用隧道连接电路
endmodule

module test (
);

  wire undriven;

  main main_1 (.Clock(undriven));  // open: Reg1_num, Reg2, Write_Reg_num, Din, Write_Enable, Reg1, Reg2_2, s0_Value, s1_Value, s2_Value, ra_Value
endmodule

module auto_count (
  input  in_1
);

  wire clk, comparator_1_eq, comparator_2_eq, not_2_out, not_3_out, not_4_out, writeback;
  wire [4:0] bit_extender_1_out, bit_extender_3_out, multiplexer_1_out;
  wire [5:0] counter_1_q;
  wire [31:0] alu_1_result, alu_2_result, bit_extender_2_out, demultiplexer_1_out0, demultiplexer_1_out1,
       demultiplexer_2_out0, demultiplexer_2_out1, main_1_reg1, multiplexer_2_out, ram_1_data, register_1_q;

  Clock clock_1 (.out(clk));
  not not_1 (writeback, counter_1_q[5]);
  Counter #(.width(6), .max('h3f), .ongoal("stay")) counter_1 (
    .load(in_1), .D({6{1'b0}}), .count(1'b1), .Q(counter_1_q), .clk(clk));  // open: carry, clr
  Bit_Extender #(.in_width(6), .out_width(5)) bit_extender_1 (.in(counter_1_q), .out(bit_extender_1_out));
  assign bit_extender_2_out = {{27{1'b0}}, bit_extender_1_out};  // Bit_Extender bit_extender_2
  // Probe on bit_extender_3_out
  Multiplexer #(.width(5), .enable("false")) multiplexer_1 (
    .in0(bit_extender_1_out), .in1(bit_extender_3_out), .out(multiplexer_1_out), .sel(counter_1_q[5]));
  ALU alu_1 (
    .AluOP(4'b0101), .X(bit_extender_2_out), .Result(alu_1_result), .Y(32'h1));  // open: Equal, Signed_Overflow, Result_2, UnSigned_Overflow
  RAM #(.addrWidth(6), .dataWidth(32), .bus("separate")) ram_1 (
    .addr(counter_1_q), .din(multiplexer_2_out), .data(ram_1_data), .str(counter_1_q[5]), .sel(1'b1),
    .clk(clk), .ld(1'b1), .clr(1'b0));
  Comparator #(.width(6)) comparator_1 (.a(counter_1_q), .b({6{1'b1}}), .eq(comparator_1_eq));  // open: gt, lt
  main main_1 (
    .Reg1_num(multiplexer_1_out), .Write_Reg_num(bit_extender_3_out), .Din(demultiplexer_2_out1),
    .Write_Enable(not_2_out), .Clock(clk), .Reg1(main_1_reg1));  // open: Reg2, Reg2_2, s0_Value, s1_Value, s2_Value, ra_Value
  not not_2 (not_2_out, counter_1_q[5]);
  Bit_Extender #(.in_width(32), .out_width(5)) bit_extender_3 (.in(alu_1_result), .out(bit_extender_3_out));
  Multiplexer #(.width(32), .enable("false")) multiplexer_2 (
    .in0(demultiplexer_1_out0), .in1(register_1_q), .out(multiplexer_2_out), .sel(comparator_1_eq));
  Demultiplexer #(.width(32)) demultiplexer_1 (
    .out0(demultiplexer_1_out0), .out1(demultiplexer_1_out1), .in(main_1_reg1), .sel(not_3_out), .en(1'b1));
  not not_3 (not_3_out, counter_1_q[5]);
  // Probe on ram_1_data
  Register #(.width(32)) register_1 (.D(demultiplexer_2_out0), .en(writeback), .Q(register_1_q), .clk(clk), .clr(1'b0));
  Comparator #(.width(6)) comparator_2 (.a(counter_1_q), .b(6'b011111), .eq(comparator_2_eq));  // open: gt, lt
  not not_4 (not_4_out, comparator_2_eq);
  // Probe on demultiplexer_2_out1
  ALU alu_2 (
    .AluOP(4'b0101), .X(ram_1_data), .Result(alu_2_result), .Y(demultiplexer_1_out1));  // open: Equal, Signed_Overflow, Result_2, UnSigned_Overflow
  Demultiplexer #(.width(32), .enable("false")) demultiplexer_2 (
    .out0(demultiplexer_2_out0), .out1(demultiplexer_2_out1), .in(alu_2_result), .sel(not_4_out));
  // Probe on demultiplexer_1_out0
  // Probe on alu_2_result
  Hex_Digit_Display hex_digit_display_1 (.value(alu_2_result[11:8]));  // open: dp
  Hex_Digit_Display hex_digit_display_2 (.value(alu_2_result[15:12]));  // open: dp
  Hex_Digit_Display hex_digit_display_3 (.value(alu_2_result[7:4]));  // open: dp
  Hex_Digit_Display hex_digit_display_4 (.value(alu_2_result[3:0]));  // open: dp
endmodule

module auto_count2 (
  input  in_1
);

  wire and_3_out, clock_1_out, comparator_1_eq, counter_2_q, ctl, ctl2, not_1_out, not_2_out;
  wire [5:0] counter_1_q;
  wire [5:5] and_1_out;
  wire [31:0] alu_1_result, demultiplexer_1_out0, demultiplexer_1_out1, main_1_reg1, ram_1_data;

  Clock clock_1 (.out(clock_1_out));
  and and_1 (and_1_out[5], ctl, counter_2_q);
  and and_2 (ctl2, ctl, counter_2_q);
  Counter #(.width(6), .max('h20), .ongoal("stay")) counter_1 (
    .load(in_1), .D({6{1'b0}}), .count(1'b1), .Q(counter_1_q), .clk(not_1_out));  // open: carry, clr
  Counter #(.width(1), .max('h1)) counter_2 (
    .load(in_1), .D(in_1), .count(1'b1), .Q(counter_2_q), .clk(clock_1_out));  // open: carry, clr
  not not_1 (not_1_out, counter_2_q);
  Demultiplexer #(.width(32), .disabled(0)) demultiplexer_1 (
    .out0(demultiplexer_1_out0), .out1(demultiplexer_1_out1), .in(main_1_reg1), .sel(counter_2_q), .en(ctl));
  RAM #(.addrWidth(6), .dataWidth(32), .bus("separate")) ram_1 (
    .addr({and_1_out[5], counter_1_q[4:0]}), .din(demultiplexer_1_out1), .data(ram_1_data), .str(ctl2),
    .sel(1'b1), .clk(clock_1_out), .ld(1'b1), .clr(in_1));
  main main_1 (
    .Reg1_num(5'b10110), .Write_Reg_num(5'b10110), .Din(alu_1_result), .Write_Enable(and_3_out),
    .Clock(clock_1_out), .Reg1(main_1_reg1));  // open: Reg2, Reg2_2, s0_Value, s1_Value, s2_Value, ra_Value
  not not_2 (not_2_out, counter_2_q);
  not not_3 (ctl, comparator_1_eq);
  Comparator #(.width(6)) comparator_1 (.a(counter_1_q), .b(6'b100000), .eq(comparator_1_eq));  // open: gt, lt
  // Probe on demultiplexer_1_out1
  and and_3 (and_3_out, not_2_out, ctl);
  Hex_Digit_Display hex_digit_display_1 (.value(alu_1_result[27:24]));  // open: dp
  Hex_Digit_Display hex_digit_display_2 (.value(alu_1_result[31:28]));  // open: dp
  ALU alu_1 (
    .AluOP(4'b0101), .X(ram_1_data), .Result(alu_1_result), .Y(demultiplexer_1_out0));  // open: Equal, Signed_Overflow, Result_2, UnSigned_Overflow
  Hex_Digit_Display hex_digit_display_3 (.value(alu_1_result[19:16]));  // open: dp
  Hex_Digit_Display hex_digit_display_4 (.value(alu_1_result[23:20]));  // open: dp
  Hex_Digit_Display hex_digit_display_5 (.value(alu_1_result[11:8]));  // open: dp
  Hex_Digit_Display hex_digit_display_6 (.value(alu_1_result[15:12]));  // open: dp
  Hex_Digit_Display hex_digit_display_7 (.value(alu_1_result[7:4]));  // open: dp
  Hex_Digit_Display hex_digit_display_8 (.value(alu_1_result[3:0]));  // open: dp
endmodule
